// Logisim project s-mips.circ as structural Verilog: 20 circuits, main circuit S-MIPS Board
module S_MIPS_Board (
  input  DESHABILITAR_DISPATCHER,
  output halt
);

  wire button_1_out, CLK, CS, d_ff_1_q, LCLR, LoadRAM, LoadRAMOn, LW, R_R_W, R_W, ram_dispatcher_1_finished,
       RCS, Reset_out, RST, TTY_EN;
  wire [2:0] KDB;
  wire [3:0] LMask, Mask, ram_1_read_time, ram_1_write_time, RMask;
  wire [6:0] KDB_DATA, TTY_DATA;
  wire [15:0] Addr, LAddr, RAddr;
  wire [31:0] I0, I1, I2, I3, LData, ram_1_data_out_0, ram_1_data_out_1, ram_1_data_out_2, ram_1_data_out_3,
       RI0, RI1, RI2, RI3;

  TTY #(.rows(25), .cols(80)) tty_1 (.data(TTY_DATA), .clk(CLK), .we(TTY_EN), .clr(RST));
  not not_1 (LoadRAMOn, ram_dispatcher_1_finished);
  RAM_Dispatcher ram_dispatcher_1 (
    .WriteTime(ram_1_write_time), .Clock(CLK), .Data(LData), .Address(LAddr), .Mask(LMask),
    .Finished(ram_dispatcher_1_finished), .Write(LW), .CLR(LCLR));
  Keyboard #(.buflen(64)) keyboard_1 (.clk(CLK), .re(KDB[0]), .avail(KDB[2]), .data(KDB_DATA));  // open: clr
  RAM ram_1 (
    .Address(RAddr), .Data_Out_0(ram_1_data_out_0), .Data_Out_1(ram_1_data_out_1),
    .Data_Out_2(ram_1_data_out_2), .Data_Out_3(ram_1_data_out_3), .Data_In_0(RI0), .Data_In_1(RI1),
    .Data_In_2(RI2), .Data_In_3(RI3), .Mask(RMask), .nRead_Write(R_R_W), .Chip_Select(RCS),
    .Read_Time(ram_1_read_time), .Reset(button_1_out), .Write_Time(ram_1_write_time));
  Button button_1 (.out(button_1_out));
  D_Flip_Flop d_ff_1 (.clk(CLK), .D(1'b1), .Q(d_ff_1_q), .reset(Reset_out));  // open: Qn, preset, en
  Button Reset (.out(Reset_out));
  S_MIPS s_mips_1 (
    .Kbd_Enable(KDB[0]), .Address(Addr), .Kbd_Clear(KDB[1]), .Kbd_Available(KDB[2]), .RAM_In_0(I0),
    .Kbd_ASCII_Data(KDB_DATA), .RAM_In_1(I1), .TTY_Enable(TTY_EN), .RAM_In_2(I2), .RAM_In_3(I3),
    .TTY_ASCII_Data(TTY_DATA), .Reset(RST), .RAM_Out_0(ram_1_data_out_0), .Clock(CLK),
    .RAM_Out_1(ram_1_data_out_1), .Stop(halt), .RAM_Out_2(ram_1_data_out_2), .RAM_Out_3(ram_1_data_out_3),
    .Mask(Mask), .Read_Time(ram_1_read_time), .Write_Time(ram_1_write_time), .nRead_Write(R_W),
    .Chip_Select(CS));
  D_Flip_Flop d_ff_2 (.clk(CLK), .D(d_ff_1_q), .Qn(LCLR), .reset(Reset_out));  // open: Q, preset, en
  or or_1 (RST, LCLR, LoadRAM);
  Clock clock_1 (.out(CLK));
  Multiplexer #(.width(32), .enable("false")) multiplexer_1 (.in0(I0), .in1(LData), .out(RI0), .sel(LoadRAM));
  Multiplexer #(.width(32), .enable("false")) multiplexer_2 (.in0(I1), .in1(LData), .out(RI1), .sel(LoadRAM));
  Multiplexer #(.width(32), .enable("false")) multiplexer_3 (.in0(I2), .in1(LData), .out(RI2), .sel(LoadRAM));
  Multiplexer #(.width(32), .enable("false")) multiplexer_4 (.in0(I3), .in1(LData), .out(RI3), .sel(LoadRAM));
  and and_1 (LoadRAM, ~DESHABILITAR_DISPATCHER, LoadRAMOn);  // AND_Gate
  Multiplexer #(.width(16), .enable("false")) multiplexer_5 (.in0(Addr), .in1(LAddr), .out(RAddr), .sel(LoadRAM));
  Multiplexer #(.width(4), .enable("false")) multiplexer_6 (.in0(Mask), .in1(LMask), .out(RMask), .sel(LoadRAM));
  Multiplexer #(.enable("false")) multiplexer_7 (.in0(CS), .in1(LW), .out(RCS), .sel(LoadRAM));
  Multiplexer #(.enable("false")) multiplexer_8 (.in0(R_W), .in1(LW), .out(R_R_W), .sel(LoadRAM));

  // Notes on the sheet:
  //   NO MODIFICAR
  //   Keyboard
endmodule

module RAM (
  input  [15:0] Address,
  input  [31:0] Data_In_0,
  input  [31:0] Data_In_1,
  input  [31:0] Data_In_2,
  input  [31:0] Data_In_3,
  input  [3:0] Mask,
  input  nRead_Write,
  input  Chip_Select,
  input  Reset,
  output [31:0] Data_Out_0,
  output [31:0] Data_Out_1,
  output [31:0] Data_Out_2,
  output [31:0] Data_Out_3,
  output [3:0] Read_Time,
  output [3:0] Write_Time
);

  wire and_2_out, and_3_out, and_4_out, and_5_out, and_6_out, and_7_out, and_8_out, and_9_out, Changed, CLK,
       comparator_2_eq, comparator_3_eq, comparator_4_eq, comparator_5_eq, comparator_6_eq, Count,
       demultiplexer_3_out0, Idle, Idle_q, Load, Load0, Load1, nand_1_out, or_1_out, or_2_out, or_3_out,
       or_4_out, or_5_out, or_6_out, or_7_out, or_8_out, or_9_out, or_10_out, Proc_q, Update_Mem, Zero_Time;
  wire [3:0] counter_1_q, multiplexer_1_out, subtractor_1_out;
  wire [31:0] register_1_q, register_2_q, register_3_q, register_4_q, register_5_q;

  // Probe on 4'b0011
  // Probe on 4'b0010
  Multiplexer #(.width(4), .enable("false")) multiplexer_1 (
    .in0(4'b0011), .in1(4'b0010), .out(multiplexer_1_out), .sel(nRead_Write));
  or or_1 (or_1_out, Idle, Update_Mem);
  or or_2 (or_2_out, ~Chip_Select, Reset);  // OR_Gate
  Subtractor #(.width(4)) subtractor_1 (.a(multiplexer_1_out), .b(4'b0010), .out(subtractor_1_out));  // open: bin, bout
  Demultiplexer #(.enable("false")) demultiplexer_1 (.out0(Idle), .out1(Load0), .in(Idle_q), .sel(Changed));
  D_Flip_Flop u_Idle (.clk(CLK), .D(or_1_out), .Q(Idle_q), .preset(or_2_out));  // open: Qn, en, reset
  // Probe on counter_1_q
  Counter #(.width(4), .max('hf)) counter_1 (
    .load(Load), .D(subtractor_1_out), .count(Count), .Q(counter_1_q), .clk(CLK), .clr(or_3_out));  // open: carry
  or or_3 (or_3_out, ~Chip_Select, Reset);  // OR_Gate
  Comparator #(.width(4), .mode("unsigned")) comparator_1 (
    .a(4'b0000), .b(counter_1_q), .eq(Zero_Time));  // open: gt, lt
  or or_4 (or_4_out, Count, Load0, Load1);
  Register #(.width(32)) register_1 (.D(Data_In_0), .en(Chip_Select), .Q(register_1_q), .clk(CLK), .clr(or_5_out));
  or or_5 (or_5_out, ~Chip_Select, Reset);  // OR_Gate
  Register #(.width(32)) register_2 (.D(Data_In_1), .en(Chip_Select), .Q(register_2_q), .clk(CLK), .clr(or_6_out));
  or or_6 (or_6_out, ~Chip_Select, Reset);  // OR_Gate
  Register #(.width(32)) register_3 (.D(Data_In_2), .en(Chip_Select), .Q(register_3_q), .clk(CLK), .clr(or_7_out));
  or or_7 (or_7_out, ~Chip_Select, Reset);  // OR_Gate
  Register #(.width(32)) register_4 (.D(Data_In_3), .en(Chip_Select), .Q(register_4_q), .clk(CLK), .clr(or_8_out));
  or or_8 (or_8_out, ~Chip_Select, Reset);  // OR_Gate
  Register #(.width(32)) register_5 (
    .D({{11{1'b1}}, nRead_Write, Mask, Address}), .en(Chip_Select), .Q(register_5_q), .clk(CLK),
    .clr(or_9_out));
  or or_9 (or_9_out, ~Chip_Select, Reset);  // OR_Gate
  D_Flip_Flop Proc (.clk(CLK), .D(or_4_out), .Q(Proc_q), .reset(or_10_out));  // open: Qn, preset, en
  or or_10 (or_10_out, ~Chip_Select, Reset);  // OR_Gate
  Demultiplexer #(.enable("false")) demultiplexer_2 (
    .out0(Count), .out1(Update_Mem), .in(demultiplexer_3_out0), .sel(Zero_Time));
  Demultiplexer #(.enable("false")) demultiplexer_3 (
    .out0(demultiplexer_3_out0), .out1(Load1), .in(Proc_q), .sel(Changed));
  Clock clock_1 (.out(CLK));
  Comparator #(.width(32)) comparator_2 (.a(register_1_q), .b(Data_In_0), .eq(comparator_2_eq));  // open: gt, lt
  Comparator #(.width(32)) comparator_3 (.a(register_2_q), .b(Data_In_1), .eq(comparator_3_eq));  // open: gt, lt
  Comparator #(.width(32)) comparator_4 (.a(register_3_q), .b(Data_In_2), .eq(comparator_4_eq));  // open: gt, lt
  Comparator #(.width(32)) comparator_5 (.a(register_4_q), .b(Data_In_3), .eq(comparator_5_eq));  // open: gt, lt
  Comparator #(.width(32)) comparator_6 (
    .a(register_5_q), .b({{11{1'b1}}, nRead_Write, Mask, Address}), .eq(comparator_6_eq));  // open: gt, lt
  nand nand_1 (nand_1_out, comparator_6_eq, comparator_2_eq, comparator_3_eq, comparator_4_eq, comparator_5_eq);
  and and_1 (Changed, nand_1_out, Chip_Select);
  or or_11 (Load, Count, Load1, Load0);
  and and_2 (and_2_out, Mask[0], Update_Mem, nRead_Write);
  and and_3 (and_3_out, Mask[1], Update_Mem, nRead_Write);
  and and_4 (and_4_out, Mask[2], Update_Mem, nRead_Write);
  and and_5 (and_5_out, Mask[3], Update_Mem, nRead_Write);
  RAM_part #(.addrWidth(16), .dataWidth(32), .bus("separate")) ram_1 (
    .addr(Address), .din(Data_In_0), .data(Data_Out_0), .str(and_2_out), .sel(Chip_Select), .clk(CLK),
    .ld(and_6_out), .clr(Reset));
  and and_6 (and_6_out, ~nRead_Write, Idle);  // AND_Gate
  RAM_part #(.addrWidth(16), .dataWidth(32), .bus("separate")) ram_2 (
    .addr(Address), .din(Data_In_1), .data(Data_Out_1), .str(and_3_out), .sel(Chip_Select), .clk(CLK),
    .ld(and_7_out), .clr(Reset));
  and and_7 (and_7_out, ~nRead_Write, Idle);  // AND_Gate
  RAM_part #(.addrWidth(16), .dataWidth(32), .bus("separate")) ram_3 (
    .addr(Address), .din(Data_In_2), .data(Data_Out_2), .str(and_4_out), .sel(Chip_Select), .clk(CLK),
    .ld(and_8_out), .clr(Reset));
  and and_8 (and_8_out, ~nRead_Write, Idle);  // AND_Gate
  RAM_part #(.addrWidth(16), .dataWidth(32), .bus("separate")) ram_4 (
    .addr(Address), .din(Data_In_3), .data(Data_Out_3), .str(and_5_out), .sel(Chip_Select), .clk(CLK),
    .ld(and_9_out), .clr(Reset));
  and and_9 (and_9_out, ~nRead_Write, Idle);  // AND_Gate

  assign Read_Time = 4'b0011;
  assign Write_Time = 4'b0010;

  // Other names for the same wires on the sheet: M0 = Mask[0]; M1 = Mask[1]; M2 = Mask[2]; M3 = Mask[3];
  //   RW = nRead_Write; CLR = Reset; CS = Chip_Select; Load2 = Count

  // Notes on the sheet:
  //   NO MODIFICAR
  //   excepto quizás los valores RT y WT
  //   BANK0
  //   BANK1
  //   BANK2
  //   BANK3
endmodule

module S_MIPS (
  input  Kbd_Available,
  input  [6:0] Kbd_ASCII_Data,
  input  [31:0] RAM_Out_0,
  input  [31:0] RAM_Out_1,
  input  Reset,
  input  [31:0] RAM_Out_2,
  input  Clock,
  input  [31:0] RAM_Out_3,
  input  [3:0] Read_Time,
  input  [3:0] Write_Time,
  output Kbd_Enable,
  output [15:0] Address,
  output Kbd_Clear,
  output TTY_Enable,
  output [6:0] TTY_ASCII_Data,
  output Stop,
  output [31:0] RAM_In_0,
  output [31:0] RAM_In_1,
  output [31:0] RAM_In_2,
  output [31:0] RAM_In_3,
  output [3:0] Mask,
  output nRead_Write,
  output Chip_Select
);

  wire data_parh_1_tty, Halt, Load_Inst, PC, PC_Addr, RAM_Inst, RAM_Read, Write;
  wire [31:0] Memory, RAM_Data, Read_RAM_mem_data;

  Read_RAM Read_RAM (
    .BANK_0(RAM_Out_0), .MEMORY(Memory), .BANK_1(RAM_Out_1), .BANK_2(RAM_Out_2), .BANK_3(RAM_Out_3),
    .MEM_DATA(Read_RAM_mem_data));
  Write_RAM write_ram_1 (
    .Data(RAM_Data), .MEMO(Memory), .MASK(Mask), .OUT_0(RAM_In_0), .OUT_1(RAM_In_1), .OUT_2(RAM_In_2),
    .OUT_3(RAM_In_3), .Addr(Address));
  Control_Unit control_unit_1 (
    .in_1(Clock), .in_2(Reset), .in_3(Read_Time), .in_4(RAM_Inst), .in_5(Write), .in_6(Halt),
    .in_7(Write_Time), .PC(PC), .Stop(Stop), .CS(Chip_Select), .Write(nRead_Write), .PC_Address(PC_Addr),
    .RAM_Read(RAM_Read), .Loading_Inst(Load_Inst));
  Data_Parh data_parh_1 (
    .in_1(Load_Inst), .Instruction(Read_RAM_mem_data), .in_4(Reset), .in_5(RAM_Read), .in_6(PC),
    .Keyboard(Kbd_ASCII_Data), .in_8(PC_Addr), .Memory(Memory), .TTY_Data(TTY_ASCII_Data),
    .Memory_Inst(RAM_Inst), .KBD(Kbd_Enable), .TTY(data_parh_1_tty), .Write_RAM(Write), .HALT(Halt),
    .RAM_Data(RAM_Data), .in_2(Clock));
  and and_1 (TTY_Enable, data_parh_1_tty, PC);

  assign Kbd_Clear = Reset;

  // Other names for the same wires on the sheet: CLK = Clock; CS = Chip_Select; KBD_AVAIL = Kbd_Available;
  //   CLR = Reset; KBD_CLR = Reset; KBD_DATA[6:0] = Kbd_ASCII_Data; RAM_A[15:0] = Address;
  //   RAM_INPUT_0[31:0] = RAM_In_0; RAM_INPUT_1[31:0] = RAM_In_1; RAM_INPUT_2[31:0] = RAM_In_2;
  //   RAM_INPUT_3[31:0] = RAM_In_3; RAM_MASK[3:0] = Mask; RAM_OUTPUT_0[31:0] = RAM_Out_0;
  //   RAM_OUTPUT_1[31:0] = RAM_Out_1; RAM_OUTPUT_2[31:0] = RAM_Out_2; RAM_OUTPUT_3[31:0] = RAM_Out_3;
  //   RW = nRead_Write; TTY_DATA[6:0] = TTY_ASCII_Data

  // Notes on the sheet:
  //   RAM ADDRESS
  //   DATA FROM RAM
  //   DATA TO RAM
  //   DATA WRITE MASK
  //   RAM TIMING
  //   RAM CONTROL
  //   KEYBOARD
  //   TTY
  //   SEQUENCING
endmodule

module RAM_Dispatcher (
  input  [3:0] WriteTime,
  input  Clock,
  input  CLR,
  output [31:0] Data,
  output [15:0] Address,
  output [3:0] Mask,
  output Finished,
  output Write
);

  wire demultiplexer_2_out1, demultiplexer_3_out1, End, IDLE_q, IncAddr, Load, or_1_out, or_2_out, While_q,
       WriteEnd;
  wire [3:0] counter_1_q;
  wire [31:0] CurrentAddress_q;

  Counter #(.width(32), .max('hffffffff)) CurrentAddress (
    .count(IncAddr), .Q({CurrentAddress_q[31:18], Address, CurrentAddress_q[1:0]}), .clk(Clock), .clr(CLR));  // open: load, D, carry
  or or_1 (or_1_out, IncAddr, demultiplexer_3_out1, Finished);
  D_Flip_Flop IDLE (.clk(Clock), .D(or_1_out), .Q(IDLE_q), .preset(CLR));  // open: Qn, en, reset
  Demultiplexer #(.enable("false")) demultiplexer_1 (.out0(Load), .out1(Finished), .in(IDLE_q), .sel(End));
  D_Flip_Flop While (.clk(Clock), .D(or_2_out), .Q(While_q), .reset(CLR));  // open: Qn, preset, en
  or or_2 (or_2_out, Write, Load);
  RAM_part #(.addrWidth(18), .dataWidth(32)) ram_1 (
    .addr({Address, CurrentAddress_q[1:0]}), .data(Data), .clk(Clock));  // open: sel, ld, clr
  Demultiplexer #(.enable("false")) demultiplexer_2 (
    .out0(Write), .out1(demultiplexer_2_out1), .in(While_q), .sel(WriteEnd));
  Decoder #(.select(2)) decoder_1 (
    .out0(Mask[0]), .out1(Mask[1]), .out2(Mask[2]), .out3(Mask[3]), .sel(CurrentAddress_q[1:0]));  // open: en
  Demultiplexer #(.enable("false")) demultiplexer_3 (
    .out0(IncAddr), .out1(demultiplexer_3_out1), .in(demultiplexer_2_out1), .sel(End));
  Counter #(.width(4), .max('hf)) counter_1 (
    .load(Load), .D(WriteTime), .count(Write), .Q(counter_1_q), .clk(Clock));  // open: carry, clr
  Comparator #(.width(32)) comparator_1 (.a(Data), .b({32{1'b1}}), .eq(End));  // open: gt, lt
  Comparator #(.width(4)) comparator_2 (.a(4'b0000), .b(counter_1_q), .eq(WriteEnd));  // open: gt, lt

  // Other names for the same wires on the sheet: CLK = Clock; Count = Write; WT[3:0] = WriteTime
endmodule

module Register_File (
  input  in_1,
  input  in_2,
  input  in_3,
  input  [31:0] Input,
  input  in_5,
  input  in_6,
  input  in_7,
  input  [4:0] in_8,
  input  [4:0] in_9,
  input  [4:0] in_10,
  output [31:0] Output,
  output [31:0] Output_2,
  output [31:0] Output_3
);

  wire input_31, L0, L1, L2, L3, L4, L5, L6, L7, L8, L9, L10, L11, L12, L13, L14, L15, L16, L17, L18, L19,
       L20, L21, L22, L23, L24, L25, L26, L27, L28, L29, L30, L31, or_1_out, or_2_out;
  wire [31:0] adder_1_out, multiplexer_1_out, multiplexer_4_out, Output19, Output_0, Output_1, Output_2_t,
       Output_3_t, Output_4, Output_5, Output_6, Output_7, Output_8, Output_9, Output_10, Output_11,
       Output_12, Output_13, Output_14, Output_15, Output_16, Output_17, Output_18, Output_19, Output_20,
       Output_21, Output_22, Output_23, Output_24, Output_25, Output_26, Output_27, Output_28, Output_29,
       Output_30, SP, subtractor_1_out;

  Multiplexer #(.width(32), .enable("false")) multiplexer_1 (
    .in0(SP), .in1(Input), .out(multiplexer_1_out), .sel(input_31));
  Demultiplexer #(.select(5), .enable("false")) demultiplexer_1 (
    .out0(L0), .out1(L1), .out2(L2), .out3(L3), .out4(L4), .out5(L5), .out6(L6), .out7(L7), .out8(L8),
    .out9(L9), .out10(L10), .out11(L11), .out12(L12), .out13(L13), .out14(L14), .out15(L15), .out16(L16),
    .out17(L17), .out18(L18), .out19(L19), .out20(L20), .out21(L21), .out22(L22), .out23(L23), .out24(L24),
    .out25(L25), .out26(L26), .out27(L27), .out28(L28), .out29(L29), .out30(L30), .out31(input_31),
    .in(in_2), .sel(in_8));
  Register #(.width(32)) R0 (.D({32{1'b0}}), .en(L0), .Q(Output_0), .clk(in_5), .clr(in_1));
  Register #(.width(32)) R7 (.D(Input), .en(L7), .Q(Output_7), .clk(in_5), .clr(in_1));
  Register #(.width(32)) R14 (.D(Input), .en(L14), .Q(Output_14), .clk(in_5), .clr(in_1));
  Register #(.width(32)) R21 (.D(Input), .en(L21), .Q(Output_21), .clk(in_5), .clr(in_1));
  Register #(.width(32)) R28 (.D(Input), .en(L28), .Q(Output_28), .clk(in_5), .clr(in_1));
  Register #(.width(32)) R31 (.D(multiplexer_1_out), .en(or_1_out), .Q(Output_3), .clk(in_5));  // open: clr
  or or_1 (or_1_out, L31, input_31, in_1);
  Register #(.width(32)) R1 (.D(Input), .en(L1), .Q(Output_1), .clk(in_5), .clr(in_1));
  Register #(.width(32)) R8 (.D(Input), .en(L8), .Q(Output_8), .clk(in_5), .clr(in_1));
  Register #(.width(32)) R15 (.D(Input), .en(L15), .Q(Output_15), .clk(in_5), .clr(in_1));
  Register #(.width(32)) R22 (.D(Input), .en(L22), .Q(Output_22), .clk(in_5), .clr(in_1));
  Register #(.width(32)) R29 (.D(Input), .en(L29), .Q(Output_29), .clk(in_5), .clr(in_1));
  or or_2 (or_2_out, in_3, in_7);
  Multiplexer #(.select(5), .width(32), .enable("false")) multiplexer_2 (
    .in0(Output_0), .in1(Output_1), .in2(Output_2_t), .in3(Output_3_t), .in4(Output_4), .in5(Output_5),
    .in6(Output_6), .in7(Output_7), .in8(Output_8), .in9(Output_9), .in10(Output_10), .in11(Output_11),
    .in12(Output_12), .in13(Output_13), .in14(Output_14), .in15(Output_15), .in16(Output_16),
    .in17(Output_17), .in18(Output_18), .in19(Output19), .in20(Output_20), .in21(Output_21),
    .in22(Output_22), .in23(Output_23), .in24(Output_24), .in25(Output_25), .in26(Output_26),
    .in27(Output_27), .in28(Output_28), .in29(Output_29), .in30(Output_30), .in31(Output_3), .out(Output),
    .sel(in_9));
  and and_1 (L31, in_6, or_2_out);
  Register #(.width(32)) R2 (.D(Input), .en(L2), .Q(Output_2_t), .clk(in_5), .clr(in_1));
  Register #(.width(32)) R9 (.D(Input), .en(L9), .Q(Output_9), .clk(in_5), .clr(in_1));
  Register #(.width(32)) R16 (.D(Input), .en(L16), .Q(Output_16), .clk(in_5), .clr(in_1));
  Register #(.width(32)) R23 (.D(Input), .en(L23), .Q(Output_23), .clk(in_5), .clr(in_1));
  Register #(.width(32)) R30 (.D(Input), .en(L30), .Q(Output_30), .clk(in_5), .clr(in_1));
  Register #(.width(32)) R3 (.D(Input), .en(L3), .Q(Output_3_t), .clk(in_5), .clr(in_1));
  Register #(.width(32)) R10 (.D(Input), .en(L10), .Q(Output_10), .clk(in_5), .clr(in_1));
  Register #(.width(32)) R17 (.D(Input), .en(L17), .Q(Output_17), .clk(in_5), .clr(in_1));
  Register #(.width(32)) R24 (.D(Input), .en(L24), .Q(Output_24), .clk(in_5), .clr(in_1));
  Subtractor #(.width(32)) subtractor_1 (.a(Output_3), .b(32'h4), .out(subtractor_1_out));  // open: bin, bout
  Adder #(.width(32)) adder_1 (.a(32'h4), .b(Output_3), .out(adder_1_out));  // open: cin, cout
  Multiplexer #(.select(5), .width(32), .enable("false")) multiplexer_3 (
    .in0(Output_0), .in1(Output_1), .in2(Output_2_t), .in3(Output_3_t), .in4(Output_4), .in5(Output_5),
    .in6(Output_6), .in7(Output_7), .in8(Output_8), .in9(Output_9), .in10(Output_10), .in11(Output_11),
    .in12(Output_12), .in13(Output_13), .in14(Output_14), .in15(Output_15), .in16(Output_16),
    .in17(Output_17), .in18(Output_18), .in19(Output19), .in20(Output_20), .in21(Output_21),
    .in22(Output_22), .in23(Output_23), .in24(Output_24), .in25(Output_25), .in26(Output_26),
    .in27(Output_27), .in28(Output_28), .in29(Output_29), .in30(Output_30), .in31(Output_3), .out(Output_2),
    .sel(in_10));
  Multiplexer #(.width(32), .enable("false")) multiplexer_4 (
    .in0(subtractor_1_out), .in1(adder_1_out), .out(multiplexer_4_out), .sel(in_7));
  Register #(.width(32)) R4 (.D(Input), .en(L4), .Q(Output_4), .clk(in_5), .clr(in_1));
  Register #(.width(32)) R11 (.D(Input), .en(L11), .Q(Output_11), .clk(in_5), .clr(in_1));
  Multiplexer #(.width(32), .enable("false")) multiplexer_5 (
    .in0(multiplexer_4_out), .in1({32{1'b1}}), .out(SP), .sel(in_1));
  Register #(.width(32)) R18 (.D(Input), .en(L18), .Q(Output_18), .clk(in_5), .clr(in_1));
  Register #(.width(32)) R25 (.D(Input), .en(L25), .Q(Output_25), .clk(in_5), .clr(in_1));
  Register #(.width(32)) R5 (.D(Input), .en(L5), .Q(Output_5), .clk(in_5), .clr(in_1));
  Register #(.width(32)) R12 (.D(Input), .en(L12), .Q(Output_12), .clk(in_5), .clr(in_1));
  Register #(.width(32)) R19 (.D(Input), .en(L19), .Q(Output_19), .clk(in_5), .clr(in_1));
  Register #(.width(32)) R26 (.D(Input), .en(L26), .Q(Output_26), .clk(in_5), .clr(in_1));
  Register #(.width(32)) R6 (.D(Input), .en(L6), .Q(Output_6), .clk(in_5), .clr(in_1));
  Register #(.width(32)) R13 (.D(Input), .en(L13), .Q(Output_13), .clk(in_5), .clr(in_1));
  Register #(.width(32)) R20 (.D(Input), .en(L20), .Q(Output_20), .clk(in_5), .clr(in_1));
  Register #(.width(32)) R27 (.D(Input), .en(L27), .Q(Output_27), .clk(in_5), .clr(in_1));

  // Other names for the same wires on the sheet: A[31:0] = Output; B[31:0] = Output_2; Clk = in_5; MemR_W = in_6;
  //   Output_31[31:0] = Output_3; Pop = in_7; Push = in_3; Reset = in_1; SelA[4:0] = in_9; SelB[4:0] = in_10;
  //   Select[4:0] = in_8; Write = in_2
endmodule

module RF_Input (
  input  [6:0] in_1,
  input  [31:0] in_2,
  input  in_3,
  input  [31:0] in_4,
  input  in_5,
  input  in_6,
  input  in_7,
  input  [31:0] in_8,
  input  in_9,
  input  in_10,
  input  [31:0] in_11,
  input  [31:0] in_12,
  output [31:0] Output
);

  wire [2:0] Selector;

  or or_1 (Selector[0], in_7, in_10, in_9);
  or or_2 (Selector[1], in_5, in_6, in_9);
  or or_3 (Selector[2], in_3, in_6, in_10);
  Multiplexer #(.select(3), .width(32), .enable("false")) multiplexer_1 (
    .in0(in_2), .in1(in_8), .in2(in_8), .in3(in_11), .in4(in_12), .in5({{25{1'b0}}, in_1}), .in6(in_4),
    .out(Output), .sel(Selector));  // open: in7

  // Other names for the same wires on the sheet: ALU[31:0] = in_2; HI[31:0] = in_11; is_kbd = in_10; is_rnd = in_9;
  //   KBD[6:0] = in_1; LO[31:0] = in_12; lw = in_3; Memory_A[31:0] = in_8; mfhi = in_6; mflo = in_7; pop = in_5;
  //   RND[31:0] = in_4
endmodule

module Instruction_Decoder (
  input  [31:0] in_1,
  output [25:0] Output,
  output [4:0] Output_2,
  output [4:0] Output_3,
  output [15:0] Output_4,
  output [4:0] Output_5,
  output Output_6,
  output Output_7,
  output Output_8,
  output Output_9,
  output Output_10,
  output Output_11,
  output Output_12,
  output Output_13,
  output Output_14,
  output Output_15,
  output Output_16,
  output Output_17,
  output Output_18,
  output Output_19,
  output Output_20,
  output Output_21,
  output Output_22,
  output Output_23,
  output Output_24,
  output Output_25,
  output Output_26,
  output Output_27,
  output Output_28,
  output Output_29,
  output Output_30,
  output Output_31,
  output Output_32,
  output Output_33,
  output Output_34,
  output Output_35,
  output Output_36,
  output Output_37,
  output Output_38,
  output Output_39,
  output Output_40,
  output Output_41
);

  wire _000000, _111111, comparator_17_eq, comparator_18_eq, comparator_19_eq, comparator_20_eq,
       comparator_21_eq, comparator_22_eq, comparator_23_eq, comparator_24_eq, comparator_25_eq,
       comparator_26_eq, comparator_27_eq, comparator_28_eq, comparator_29_eq, comparator_30_eq,
       comparator_31_eq, comparator_32_eq, comparator_33_eq, comparator_34_eq, comparator_35_eq,
       comparator_36_eq, comparator_37_eq, comparator_38_eq, comparator_39_eq, comparator_40_eq;

  Comparator #(.width(6)) comparator_1 (.a(in_1[31:26]), .b(6'b001000), .eq(Output_6));  // open: gt, lt
  Comparator #(.width(6)) comparator_2 (.a(in_1[31:26]), .b(6'b001010), .eq(Output_8));  // open: gt, lt
  Comparator #(.width(6)) comparator_3 (.a(in_1[31:26]), .b(6'b001011), .eq(Output_12));  // open: gt, lt
  Comparator #(.width(6)) comparator_4 (.a(in_1[31:26]), .b(6'b001100), .eq(Output_16));  // open: gt, lt
  Comparator #(.width(6)) comparator_5 (.a(in_1[31:26]), .b(6'b001101), .eq(Output_20));  // open: gt, lt
  Comparator #(.width(6)) comparator_6 (.a(in_1[31:26]), .b(6'b001110), .eq(Output_24));  // open: gt, lt
  Comparator #(.width(6)) comparator_7 (.a(in_1[31:26]), .b(6'b100011), .eq(Output_28));  // open: gt, lt
  Comparator #(.width(6)) comparator_8 (.a(in_1[31:26]), .b(6'b000010), .eq(Output_37));  // open: gt, lt
  Comparator #(.width(6)) comparator_9 (.a(in_1[31:26]), .b(6'b101011), .eq(Output_7));  // open: gt, lt
  Comparator #(.width(6)) comparator_10 (.a(in_1[31:26]), .b(6'b000100), .eq(Output_9));  // open: gt, lt
  Comparator #(.width(6)) comparator_11 (.a(in_1[31:26]), .b(6'b000101), .eq(Output_13));  // open: gt, lt
  Comparator #(.width(6)) comparator_12 (.a(in_1[31:26]), .b(6'b000110), .eq(Output_17));  // open: gt, lt
  Comparator #(.width(6)) comparator_13 (.a(in_1[31:26]), .b(6'b000111), .eq(Output_21));  // open: gt, lt
  Comparator #(.width(6)) comparator_14 (.a(in_1[31:26]), .b(6'b000001), .eq(Output_25));  // open: gt, lt
  Comparator #(.width(6)) comparator_15 (.a(in_1[31:26]), .b({6{1'b1}}), .eq(_111111));  // open: gt, lt
  Comparator #(.width(6)) comparator_16 (.a(in_1[31:26]), .b({6{1'b0}}), .eq(_000000));  // open: gt, lt
  Comparator #(.width(6)) comparator_17 (.a(in_1[5:0]), .b({6{1'b0}}), .eq(comparator_17_eq));  // open: gt, lt
  Comparator #(.width(6)) comparator_18 (.a(in_1[5:0]), .b(6'b100000), .eq(comparator_18_eq));  // open: gt, lt
  Comparator #(.width(6)) comparator_19 (.a(in_1[5:0]), .b(6'b100010), .eq(comparator_19_eq));  // open: gt, lt
  Comparator #(.width(6)) comparator_20 (.a(in_1[5:0]), .b(6'b011000), .eq(comparator_20_eq));  // open: gt, lt
  Comparator #(.width(6)) comparator_21 (.a(in_1[5:0]), .b(6'b011001), .eq(comparator_21_eq));  // open: gt, lt
  Comparator #(.width(6)) comparator_22 (.a(in_1[5:0]), .b(6'b011010), .eq(comparator_22_eq));  // open: gt, lt
  Comparator #(.width(6)) comparator_23 (.a(in_1[5:0]), .b(6'b011011), .eq(comparator_23_eq));  // open: gt, lt
  Comparator #(.width(6)) comparator_24 (.a(in_1[5:0]), .b(6'b101010), .eq(comparator_24_eq));  // open: gt, lt
  Comparator #(.width(6)) comparator_25 (.a(in_1[31:26]), .b(6'b111000), .eq(comparator_25_eq));  // open: gt, lt
  Comparator #(.width(6)) comparator_26 (.a(in_1[5:0]), .b({6{1'b0}}), .eq(comparator_26_eq));  // open: gt, lt
  Comparator #(.width(6)) comparator_27 (.a(in_1[31:26]), .b(6'b111000), .eq(comparator_27_eq));  // open: gt, lt
  Comparator #(.width(6)) comparator_28 (.a(in_1[5:0]), .b(6'b000001), .eq(comparator_28_eq));  // open: gt, lt
  and and_1 (Output_10, _000000, comparator_17_eq);
  and and_2 (Output_14, _000000, comparator_18_eq);
  and and_3 (Output_18, _000000, comparator_19_eq);
  and and_4 (Output_22, _000000, comparator_20_eq);
  and and_5 (Output_26, _000000, comparator_21_eq);
  and and_6 (Output_29, _000000, comparator_22_eq);
  and and_7 (Output_31, _000000, comparator_23_eq);
  and and_8 (Output_33, _000000, comparator_24_eq);
  and and_9 (Output_35, comparator_25_eq, comparator_26_eq);
  and and_10 (Output_38, comparator_27_eq, comparator_28_eq);
  Comparator #(.width(6)) comparator_29 (.a(in_1[5:0]), .b(6'b101011), .eq(comparator_29_eq));  // open: gt, lt
  Comparator #(.width(6)) comparator_30 (.a(in_1[5:0]), .b(6'b100100), .eq(comparator_30_eq));  // open: gt, lt
  Comparator #(.width(6)) comparator_31 (.a(in_1[5:0]), .b(6'b100101), .eq(comparator_31_eq));  // open: gt, lt
  Comparator #(.width(6)) comparator_32 (.a(in_1[5:0]), .b(6'b100111), .eq(comparator_32_eq));  // open: gt, lt
  Comparator #(.width(6)) comparator_33 (.a(in_1[5:0]), .b(6'b101000), .eq(comparator_33_eq));  // open: gt, lt
  Comparator #(.width(6)) comparator_34 (.a(in_1[5:0]), .b(6'b001000), .eq(comparator_34_eq));  // open: gt, lt
  Comparator #(.width(6)) comparator_35 (.a(in_1[5:0]), .b(6'b010000), .eq(comparator_35_eq));  // open: gt, lt
  Comparator #(.width(6)) comparator_36 (.a(in_1[5:0]), .b(6'b010010), .eq(comparator_36_eq));  // open: gt, lt
  Comparator #(.width(6)) comparator_37 (.a(in_1[5:0]), .b({6{1'b1}}), .eq(comparator_37_eq));  // open: gt, lt
  Comparator #(.width(6)) comparator_38 (.a(in_1[5:0]), .b(6'b000001), .eq(comparator_38_eq));  // open: gt, lt
  Comparator #(.width(6)) comparator_39 (.a(in_1[5:0]), .b(6'b000010), .eq(comparator_39_eq));  // open: gt, lt
  Comparator #(.width(6)) comparator_40 (.a(in_1[5:0]), .b(6'b000100), .eq(comparator_40_eq));  // open: gt, lt
  and and_11 (Output_11, _000000, comparator_29_eq);
  and and_12 (Output_15, _000000, comparator_30_eq);
  and and_13 (Output_19, _000000, comparator_31_eq);
  and and_14 (Output_23, _000000, comparator_32_eq);
  and and_15 (Output_27, _000000, comparator_33_eq);
  and and_16 (Output_30, _000000, comparator_34_eq);
  and and_17 (Output_32, _000000, comparator_35_eq);
  and and_18 (Output_34, _000000, comparator_36_eq);
  and and_19 (Output_36, _111111, comparator_37_eq);
  and and_20 (Output_40, _111111, comparator_38_eq);
  and and_21 (Output_39, _111111, comparator_39_eq);
  and and_22 (Output_41, _111111, comparator_40_eq);

  assign Output = in_1[25:0];
  assign Output_2 = in_1[25:21];
  assign Output_3 = in_1[20:16];
  assign Output_4 = in_1[15:0];
  assign Output_5 = in_1[15:11];

  // Other names for the same wires on the sheet: add = Output_14; addi = Output_6; and = Output_15; andi = Output_16;
  //   beq = Output_9; bgtz = Output_21; blez = Output_17; bltz = Output_25; bne = Output_13; div = Output_29;
  //   divu = Output_31; halt = Output_36; constant[15:0] = in_1[15:0]; dest[25:0] = in_1[25:0]; FC[5:0] = in_1[5:0];
  //   RD[4:0] = in_1[15:11]; RT[4:0] = in_1[20:16]; RS[4:0] = in_1[25:21]; OP[5:0] = in_1[31:26]; j = Output_37;
  //   jr = Output_30; kbd = Output_41; lw = Output_28; mfhi = Output_32; mflo = Output_34; mult = Output_22;
  //   mulu = Output_26; nop = Output_10; nor = Output_23; or = Output_19; ori = Output_20; pop = Output_35;
  //   push = Output_38; rnd = Output_39; slt = Output_33; slti = Output_8; sltiu = Output_12; sltu = Output_11;
  //   sub = Output_18; sw = Output_7; tty = Output_40; xor = Output_27; xori = Output_24

  // Notes on the sheet:
  //   Instrucciones Tipo J
  //   Instrucciones Tipo I
  //   Instrucciones Tipo R
endmodule

module Multiplier (
  input  [31:0] X,
  input  [31:0] Y,
  output [31:0] High_Output,
  output [31:0] Low_Output
);

  wire [31:0] adder_1_out, multiplexer_1_out, multiplexer_2_out, multiplier_1_cout;

  Multiplexer #(.width(32), .enable("false")) multiplexer_1 (
    .in0({32{1'b0}}), .in1(X), .out(multiplexer_1_out), .sel(Y[31]));
  Multiplexer #(.width(32), .enable("false")) multiplexer_2 (
    .in0({32{1'b0}}), .in1(Y), .out(multiplexer_2_out), .sel(X[31]));
  Multiplier_part #(.width(32)) multiplier_1 (.a(X), .b(Y), .out(Low_Output), .cout(multiplier_1_cout));  // open: cin
  Adder #(.width(32)) adder_1 (.a(multiplexer_1_out), .b(multiplexer_2_out), .out(adder_1_out));  // open: cin, cout
  // Probe on Low_Output
  Adder #(.width(32)) adder_2 (.a(multiplier_1_cout), .b(adder_1_out), .out(High_Output));  // open: cin, cout
  // Probe on Low_Output
endmodule

module Signed_Divider (
  input  [31:0] X,
  input  [31:0] Y,
  output [31:0] High_Output,
  output [31:0] LowOutput
);

  wire xor_1_out;
  wire [31:0] divider_1_out, multiplexer_1_out, multiplexer_2_out, negator_1_out, negator_2_out,
       negator_3_out;

  Negator #(.width(32)) negator_1 (.in(X), .out(negator_1_out));
  Multiplexer #(.width(32), .enable("false")) multiplexer_1 (
    .in0(X), .in1(negator_1_out), .out(multiplexer_1_out), .sel(X[31]));
  Multiplexer #(.width(32), .enable("false")) multiplexer_2 (
    .in0(Y), .in1(negator_2_out), .out(multiplexer_2_out), .sel(Y[31]));
  Negator #(.width(32)) negator_2 (.in(Y), .out(negator_2_out));
  Divider #(.width(32)) divider_1 (
    .a(multiplexer_1_out), .b(multiplexer_2_out), .out(divider_1_out), .rem(High_Output));  // open: upper
  xor xor_1 (xor_1_out, X[31], Y[31]);
  Multiplexer #(.width(32), .enable("false")) multiplexer_3 (
    .in0(divider_1_out), .in1(negator_3_out), .out(LowOutput), .sel(xor_1_out));
  Negator #(.width(32)) negator_3 (.in(divider_1_out), .out(negator_3_out));
  // Probe on LowOutput
  // Probe on High_Output
endmodule

module Program_Counter (
  input  in_1,
  input  in_2,
  input  in_3,
  input  [31:0] Input,
  output [31:0] Output
);

  Register #(.width(32)) register_1 (.D(Input), .en(in_2), .Q(Output), .clk(in_1), .clr(in_3));

  // Other names for the same wires on the sheet: Clock = in_1; Enable = in_2; Reset = in_3
endmodule

module ALU_Encoder (
  input  ADD,
  input  ADDI,
  input  SUB,
  input  MULT,
  input  MULU,
  input  DIV,
  input  DIVU,
  input  SLT,
  input  SLTI,
  input  SLTU,
  input  SLTUI,
  input  AND,
  input  ANDI,
  input  OR,
  input  ORI,
  input  XOR,
  input  XORI,
  input  NOR,
  output TYPE_I,
  output [3:0] ALU_SELECTOR
);

  wire ADD_t, AND_t, OR_t, SLT_t, SLTU_t, XOR_t;

  or or_1 (ADD_t, ADD, ADDI);
  or or_2 (SLT_t, SLT, SLTI);
  or or_3 (SLTU_t, SLTU, SLTUI);
  or or_4 (AND_t, AND, ANDI);
  or or_5 (OR_t, OR, ORI);
  or or_6 (XOR_t, XOR, XORI);
  ExactlyOne xor_1 (.out(TYPE_I), .in0(ADDI), .in1(SLTI), .in2(SLTUI), .in3(ANDI), .in4(ORI), .in5(XORI));
  ExactlyOne xor_2 (.out(ALU_SELECTOR[3]), .in0(MULT), .in1(DIVU), .in2(DIV), .in3(MULU));
  ExactlyOne xor_3 (.out(ALU_SELECTOR[2]), .in0(SLT_t), .in1(SLTU_t), .in2(ADD_t), .in3(SUB));
  ExactlyOne xor_4 (.out(ALU_SELECTOR[1]), .in0(NOR), .in1(XOR_t), .in2(ADD_t), .in3(SUB), .in4(DIV), .in5(MULU));
  ExactlyOne xor_5 (.out(ALU_SELECTOR[0]), .in0(OR_t), .in1(XOR_t), .in2(SLTU_t), .in3(SUB), .in4(DIVU), .in5(MULU));
endmodule

module ALU (
  input  [3:0] Selector,
  input  [31:0] X,
  input  [31:0] Y,
  input  CLK,
  output [31:0] ALU_Output,
  output ZF,
  output SF,
  output [31:0] HIGH,
  output [31:0] LOW
);

  wire comparator_1_lt, comparator_2_lt, ENABLE_HIGH_LOW;
  wire [1:0] Selector_MUL_DIV;
  wire [31:0] ADD, AND, divider_1_out, divider_1_rem, multiplexer_2_out, multiplexer_3_out,
       multiplier_1_cout, multiplier_1_out, multiplier_2_high_output, multiplier_2_low_output, NOR, OR,
       signed_divider_1_high_output, signed_divider_1_lowoutput, SLT, SLTU, SUB, XOR;

  assign AND = X & Y;  // AND_Gate and_1, 32 bits wide
  assign OR = X | Y;  // OR_Gate or_1, 32 bits wide
  assign XOR = X ^ Y;  // XOR_Gate xor_1, 32 bits wide
  assign NOR = ~(X | Y);  // NOR_Gate nor_1, 32 bits wide
  Comparator #(.width(32)) comparator_1 (.a(X), .b(Y), .lt(comparator_1_lt));  // open: gt, eq
  Comparator #(.width(32), .mode("unsigned")) comparator_2 (.a(X), .b(Y), .lt(comparator_2_lt));  // open: gt, eq
  Adder #(.width(32)) adder_1 (.a(X), .b(Y), .out(ADD));  // open: cin, cout
  Subtractor #(.width(32)) subtractor_1 (.a(X), .b(Y), .out(SUB));  // open: bin, bout
  assign SLT = {{31{1'b0}}, comparator_1_lt};  // Bit_Extender bit_extender_1
  assign SLTU = {{31{1'b0}}, comparator_2_lt};  // Bit_Extender bit_extender_2
  Multiplexer #(.select(4), .width(32), .enable("false")) multiplexer_1 (
    .in0(AND), .in1(OR), .in2(NOR), .in3(XOR), .in4(SLT), .in5(SLTU), .in6(ADD), .in7(SUB), .out(ALU_Output),
    .sel(Selector));  // open: in8, in9, in10, in11, in12, in13, in14, in15
  Multiplier_part #(.width(32)) multiplier_1 (
    .a(X), .b(Y), .out(multiplier_1_out), .cout(multiplier_1_cout));  // open: cin
  Divider #(.width(32)) divider_1 (.a(X), .b(Y), .out(divider_1_out), .rem(divider_1_rem));  // open: upper
  Signed_Divider signed_divider_1 (
    .X(X), .Y(Y), .High_Output(signed_divider_1_high_output), .LowOutput(signed_divider_1_lowoutput));
  Multiplier multiplier_2 (.X(X), .Y(Y), .High_Output(multiplier_2_high_output), .Low_Output(multiplier_2_low_output));
  Comparator #(.width(32)) comparator_3 (.a(ALU_Output), .b({32{1'b1}}), .eq(ZF), .lt(SF));  // open: gt
  Multiplexer #(.select(2), .width(32), .enable("false")) multiplexer_2 (
    .in0(multiplier_1_cout), .in1(divider_1_rem), .in2(signed_divider_1_high_output),
    .in3(multiplier_2_high_output), .out(multiplexer_2_out), .sel(Selector_MUL_DIV));
  Multiplexer #(.select(2), .width(32), .enable("false")) multiplexer_3 (
    .in0(multiplier_1_out), .in1(divider_1_out), .in2(signed_divider_1_lowoutput),
    .in3(multiplier_2_low_output), .out(multiplexer_3_out), .sel(Selector_MUL_DIV));
  Register #(.width(32)) register_1 (.D(multiplexer_2_out), .en(ENABLE_HIGH_LOW), .Q(HIGH), .clk(CLK));  // open: clr
  Register #(.width(32)) register_2 (.D(multiplexer_3_out), .en(ENABLE_HIGH_LOW), .Q(LOW), .clk(CLK));  // open: clr
  and and_2 (ENABLE_HIGH_LOW, Selector[3], ~Selector[2]);  // AND_Gate
  and and_3 (Selector_MUL_DIV[1], Selector[3], ~Selector[2], Selector[1]);  // AND_Gate
  and and_4 (Selector_MUL_DIV[0], Selector[3], ~Selector[2], Selector[0]);  // AND_Gate
endmodule

module Timer (
  input  [3:0] Time,
  input  Start,
  input  CLK,
  input  Reset,
  output Output
);

  wire [3:0] counter_1_q;

  Counter #(.width(4), .max('hf)) counter_1 (
    .count(Start), .Q(counter_1_q), .clk(CLK), .clr(Reset));  // open: load, D, carry
  Comparator #(.width(4)) comparator_1 (.a(Time), .b(counter_1_q), .eq(Output));  // open: gt, lt
endmodule

module Branch_Control (
  input  [31:0] ALU,
  input  [15:0] Offset,
  input  [31:0] PC,
  input  [25:0] Dest,
  input  [31:0] RS,
  input  [31:0] RT,
  input  BEQ,
  input  BNE,
  input  BLEZ,
  input  BGTZ,
  input  BLTZ,
  input  is_J,
  input  is_JR,
  output [31:0] OUT
);

  wire and_1_out, and_2_out, and_3_out, and_4_out, and_5_out, Branch_Taken, comparator_1_eq, comparator_1_lt,
       comparator_2_eq, or_3_out;
  wire [1:0] or_1_out;
  wire [31:0] _32bit_Offset, _32bit_Offset_x_4, Offset_Target, PC___4, RS_t;

  assign _32bit_Offset = {{16{Offset[15]}}, Offset};  // Bit_Extender bit_extender_1
  Shifter #(.width(32)) shifter_1 (.in(_32bit_Offset), .\dist (5'b00010), .out(_32bit_Offset_x_4));
  Adder #(.width(32)) adder_1 (.a(PC___4), .b(_32bit_Offset_x_4), .out(Offset_Target));  // open: cin, cout
  Adder #(.width(32)) adder_2 (.a(PC), .b(32'h4), .out(PC___4));  // open: cin, cout
  Multiplexer #(.select(2), .width(32), .enable("false")) multiplexer_1 (
    .in0(PC___4), .in1(Offset_Target), .in2({PC[31:28], Dest, 2'b00}), .in3(RS_t), .out(OUT), .sel(or_1_out));
  or or_1 (or_1_out[0], is_JR, Branch_Taken);
  or or_2 (or_1_out[1], is_J, is_JR);
  Comparator #(.width(32)) comparator_1 (
    .a(RS), .b({32{1'b0}}), .eq(comparator_1_eq), .lt(comparator_1_lt));  // open: gt
  Comparator #(.width(32)) comparator_2 (.a(RS), .b(RT), .eq(comparator_2_eq));  // open: gt, lt
  or or_3 (or_3_out, comparator_1_eq, comparator_1_lt);
  and and_1 (and_1_out, BEQ, comparator_2_eq);
  and and_2 (and_2_out, ~comparator_2_eq, BNE);  // AND_Gate
  and and_3 (and_3_out, BLEZ, or_3_out);
  and and_4 (and_4_out, ~or_3_out, BGTZ);  // AND_Gate
  and and_5 (and_5_out, BLTZ, comparator_1_lt);
  or or_4 (Branch_Taken, and_1_out, and_2_out, and_3_out, and_4_out, and_5_out);

  // Other names for the same wires on the sheet: _16bit_Offset[15:0] = Offset; J = is_J; JR = is_JR;
  //   Jump_Target[31:2] = {PC[31:28], Dest}
endmodule

module Read_RAM (
  input  [31:0] BANK_0,
  input  [31:0] MEMORY,
  input  [31:0] BANK_1,
  input  [31:0] BANK_2,
  input  [31:0] BANK_3,
  output [31:0] MEM_DATA
);

  Multiplexer #(.select(2), .width(32), .enable("false")) multiplexer_1 (
    .in0(BANK_0), .in1(BANK_1), .in2(BANK_2), .in3(BANK_3), .out(MEM_DATA), .sel(MEMORY[3:2]));

  // Other names for the same wires on the sheet: Selector[1:0] = MEMORY[3:2]
endmodule

module Data_Parh (
  input  in_1,
  input  in_2,
  input  [31:0] Instruction,
  input  in_4,
  input  in_5,
  input  in_6,
  input  [6:0] Keyboard,
  input  in_8,
  output [31:0] Memory,
  output [6:0] TTY_Data,
  output Memory_Inst,
  output KBD,
  output Write_RAM,
  output TTY,
  output HALT,
  output [31:0] RAM_Data
);

  wire add, addi, \and , and_1_out, and_2_out, andi, beq, bgtz, blez, bltz, bne, div, divu, j, jr, lw, mfhi,
       mflo, mult, mulu, nop, \nor , \or , or_1_out, or_2_out, or_3_out, or_5_out, ori, pop, push, RF_Write,
       rnd, SF, slt, slti, sltiu, sltu, sub, sw, Type_I, \xor , xori, ZF;
  wire [3:0] alu_encoder_1_alu_selector;
  wire [4:0] multiplexer_3_out, RD, RS, RT;
  wire [15:0] \const ;
  wire [25:0] dest;
  wire [31:0] ALU, bit_extender_1_out, bit_extender_2_out, branch_control_1_out, HI, LO, multiplexer_1_out,
       multiplexer_2_out, PC, random_1_out, register_1_q, rf_input_1_output, RT_t, SP;
  wire [31:7] RS_t;

  Register #(.width(32)) register_1 (.D(Instruction), .en(in_1), .Q(register_1_q), .clk(in_2), .clr(in_4));
  Instruction_Decoder instruction_decoder_1 (
    .Output(dest), .Output_2(RS), .Output_3(RT), .in_1(register_1_q), .Output_4(\const ), .Output_5(RD),
    .Output_6(addi), .Output_7(sw), .Output_8(slti), .Output_9(beq), .Output_10(nop), .Output_11(sltu),
    .Output_12(sltiu), .Output_13(bne), .Output_14(add), .Output_15(\and ), .Output_16(andi),
    .Output_17(blez), .Output_18(sub), .Output_19(\or ), .Output_20(ori), .Output_21(bgtz), .Output_22(mult),
    .Output_23(\nor ), .Output_24(xori), .Output_25(bltz), .Output_26(mulu), .Output_27(\xor ),
    .Output_28(lw), .Output_29(div), .Output_30(jr), .Output_31(divu), .Output_32(mfhi), .Output_33(slt),
    .Output_34(mflo), .Output_35(pop), .Output_36(HALT), .Output_37(j), .Output_38(push), .Output_39(rnd),
    .Output_40(TTY), .Output_41(KBD));
  or or_1 (or_1_out, sw, addi, lw);
  or or_2 (or_2_out, add, \and , ori, sub, \or , xori, rnd, \nor , mfhi, \xor , mflo, addi, KBD, slti, slt, sltiu, sltu, andi);
  Program_Counter program_counter_1 (.in_1(in_2), .in_3(in_4), .Output(PC));  // open: in_2, Input
  and and_1 (and_1_out, in_6, or_2_out);
  or or_3 (or_3_out, lw, pop);
  and and_2 (and_2_out, or_3_out, in_5);
  ALU_Encoder alu_encoder_1 (
    .ADD(add), .ADDI(or_1_out), .SUB(sub), .MULT(mult), .MULU(mulu), .DIV(div), .DIVU(divu), .SLT(slt),
    .SLTI(slti), .SLTU(sltu), .SLTUI(sltiu), .AND(\and ), .ANDI(andi), .OR(\or ), .ORI(ori), .XOR(\xor ),
    .XORI(xori), .NOR(\nor ), .TYPE_I(Type_I), .ALU_SELECTOR(alu_encoder_1_alu_selector));
  Random #(.width(32)) random_1 (.clk(in_2), .next(in_4), .out(random_1_out));  // open: clr
  or or_4 (RF_Write, and_1_out, and_2_out);
  assign bit_extender_1_out = {{16{1'b0}}, \const };  // Bit_Extender bit_extender_1
  or or_5 (or_5_out, andi, ori, xori);
  assign bit_extender_2_out = {{16{\const [15]}}, \const };  // Bit_Extender bit_extender_2
  Multiplexer #(.width(32), .enable("false")) multiplexer_1 (
    .in0(RT_t), .in1(multiplexer_2_out), .out(multiplexer_1_out), .sel(Type_I));
  Multiplexer #(.width(32), .enable("false")) multiplexer_2 (
    .in0(bit_extender_1_out), .in1(bit_extender_2_out), .out(multiplexer_2_out), .sel(or_5_out));
  RF_Input rf_input_1 (
    .in_1(Keyboard), .in_2(ALU), .in_3(lw), .in_4(random_1_out), .in_5(pop), .in_6(mfhi), .in_7(mflo),
    .in_8(Instruction), .in_9(rnd), .in_10(KBD), .Output(rf_input_1_output));  // open: in_11, in_12
  Branch_Control branch_control_1 (
    .ALU(ALU), .Offset(\const ), .PC(PC), .Dest(dest), .RS({RS_t, TTY_Data}), .BEQ(beq), .BNE(bne),
    .BLEZ(blez), .BGTZ(bgtz), .BLTZ(bltz), .is_J(j), .is_JR(jr), .OUT(branch_control_1_out), .RT(RT_t));
  Multiplexer #(.width(5), .enable("false")) multiplexer_3 (.in0(RD), .in1(RT), .out(multiplexer_3_out), .sel(Type_I));
  ALU alu_1 (
    .Selector(alu_encoder_1_alu_selector), .X({RS_t, TTY_Data}), .Y(multiplexer_1_out), .HIGH(HI), .LOW(LO),
    .CLK(in_2), .ALU_Output(ALU), .ZF(ZF), .SF(SF));
  Register_File register_file_1 (
    .in_1(in_4), .in_2(RF_Write), .in_3(push), .Input(rf_input_1_output), .in_6(in_6), .in_7(pop),
    .in_8(multiplexer_3_out), .in_9(RS), .in_10(RT), .Output({RS_t, TTY_Data}), .Output_2(RT_t),
    .Output_3(SP), .in_5(in_2));
  or or_6 (Write_RAM, sw, push);
  Program_Counter program_counter_2 (.in_1(in_2), .in_2(in_6), .in_3(in_4), .Input(branch_control_1_out), .Output(PC));
  Multiplexer #(.width(32), .enable("false")) multiplexer_4 (
    .in0({RS_t, TTY_Data}), .in1(RT_t), .out(RAM_Data), .sel(sw));
  or or_7 (Memory_Inst, lw, Write_RAM, pop);
  Memory_Address memory_address_1 (
    .Pop(pop), .Push(push), .ALU(ALU), .PC(PC), .SP(SP), .LW(lw), .SW(sw), .in_8(in_8), .OUT(Memory));

  // Other names for the same wires on the sheet: CLK = in_2; En_PC = in_6; Inst[31:0] = Instruction;
  //   KBD_t[6:0] = Keyboard; LD_INST = in_1; PC_Addr = in_8; RAM_Read = in_5; Reset = in_4; RS_t[6:0] = TTY_Data
endmodule

module LE_to_BE (
  input  [31:0] IN,
  input  [3:0] in_2,
  input  [31:0] IN_3,
  input  [31:0] IN_4,
  output [31:0] OUT,
  output [31:0] Output
);

  ALU alu_1 (.Selector(in_2), .X(IN_3), .Y(IN_4), .ALU_Output(Output));  // open: HIGH, LOW, CLK, ZF, SF

  assign OUT = {IN[7:0], IN[15:8], IN[23:16], IN[31:24]};
endmodule

module Write_RAM (
  input  [31:0] Data,
  input  [31:0] MEMO,
  output [3:0] MASK,
  output [31:0] OUT_0,
  output [31:0] OUT_1,
  output [31:0] OUT_2,
  output [31:0] OUT_3,
  output [15:0] Addr
);

  wire [31:0] le_to_be_1_out;

  Demultiplexer #(.select(2), .enable("false")) demultiplexer_1 (
    .out0(MASK[0]), .out1(MASK[1]), .out2(MASK[2]), .out3(MASK[3]), .in(1'b1), .sel(MEMO[3:2]));
  LE_to_BE le_to_be_1 (.IN(Data), .OUT(le_to_be_1_out));  // open: Output, in_2, IN_3, IN_4
  Demultiplexer #(.select(2), .width(32), .enable("false")) demultiplexer_2 (
    .out0(OUT_0), .out1(OUT_1), .out2(OUT_2), .out3(OUT_3), .in(le_to_be_1_out), .sel(MEMO[3:2]));

  assign Addr = MEMO[19:4];

  // Other names for the same wires on the sheet: SELECTOR[1:0] = MEMO[3:2]
endmodule

module Memory_Address (
  input  Pop,
  input  Push,
  input  [31:0] ALU,
  input  [31:0] PC,
  input  [31:0] SP,
  input  LW,
  input  SW,
  input  in_8,
  output [31:0] OUT
);

  wire [1:0] or_2_out;
  wire [31:0] multiplexer_1_out, subtractor_1_out;

  Subtractor #(.width(32)) subtractor_1 (.a(SP), .b(32'h4), .out(subtractor_1_out));  // open: bin, bout
  Multiplexer #(.width(32), .enable("false")) multiplexer_1 (
    .in0(SP), .in1(subtractor_1_out), .out(multiplexer_1_out), .sel(Push));
  or or_1 (or_2_out[1], Push, Pop, in_8);
  Multiplexer #(.select(2), .width(32), .enable("false")) multiplexer_2 (
    .in0(PC), .in1(ALU), .in2(multiplexer_1_out), .in3(PC), .out(OUT), .sel(or_2_out));
  or or_2 (or_2_out[0], in_8, LW, SW);

  // Other names for the same wires on the sheet: PC_Addr = in_8
endmodule

module Control_Unit (
  input  in_1,
  input  in_2,
  input  [3:0] in_3,
  input  in_4,
  input  in_5,
  input  in_6,
  input  [3:0] in_7,
  output PC,
  output Loading_Inst,
  output Stop,
  output RAM_Read,
  output CS,
  output Write,
  output PC_Address
);

  wire Chip_1, Chip_2, demultiplexer_1_out1, demultiplexer_2_out0, demultiplexer_3_out0,
       demultiplexer_4_out0, demultiplexer_5_out0, IDLE_q, Loading_Inst_q, or_2_out, or_3_out, or_4_out,
       or_5_out, RAM, RAM_Read_t, Stop_t, timer_1_output, timer_2_output, Timer__Reset;
  wire [3:0] multiplexer_1_out;

  or or_1 (PC, demultiplexer_5_out0, RAM_Read_t);
  or or_2 (or_2_out, demultiplexer_2_out0, RAM);
  Multiplexer #(.width(4), .enable("false")) multiplexer_1 (
    .in0(in_3), .in1(in_7), .out(multiplexer_1_out), .sel(in_5));
  or or_3 (or_3_out, demultiplexer_5_out0, RAM_Read_t, demultiplexer_1_out1);
  D_Flip_Flop #(.trigger("falling")) IDLE (.clk(in_1), .D(or_3_out), .Q(IDLE_q), .preset(in_2));  // open: Qn, en, reset
  Demultiplexer #(.enable("false")) demultiplexer_1 (
    .out0(Timer__Reset), .out1(demultiplexer_1_out1), .in(IDLE_q), .sel(in_2));
  D_Flip_Flop #(.trigger("falling")) RAM_Waiter (.clk(in_1), .D(or_2_out), .Q(Chip_2));  // open: Qn, preset, en, reset
  Demultiplexer #(.enable("false")) demultiplexer_2 (
    .out0(demultiplexer_2_out0), .out1(RAM_Read), .in(Chip_2), .sel(timer_1_output));
  Timer timer_1 (.Start(in_1), .Output(timer_1_output), .Time(multiplexer_1_out), .CLK(1'b1), .Reset(RAM));
  or or_4 (or_4_out, demultiplexer_3_out0, Timer__Reset);
  D_Flip_Flop #(.trigger("falling")) Loading (
    .clk(in_1), .D(RAM_Read), .Q(RAM_Read_t), .reset(in_2));  // open: Qn, preset, en
  Demultiplexer #(.enable("false")) demultiplexer_3 (
    .out0(demultiplexer_3_out0), .out1(Loading_Inst), .in(Chip_1), .sel(timer_2_output));
  D_Flip_Flop #(.trigger("falling")) Read_Waiter (.clk(in_1), .D(or_4_out), .Q(Chip_1));  // open: Qn, preset, en, reset
  Timer timer_2 (.Start(in_1), .Output(timer_2_output), .Time(in_3), .CLK(1'b1), .Reset(Timer__Reset));
  or or_5 (or_5_out, Stop, Stop_t);
  D_Flip_Flop #(.trigger("falling")) u_Loading_Inst (
    .clk(in_1), .D(Loading_Inst), .Q(Loading_Inst_q), .reset(in_2));  // open: Qn, preset, en
  Demultiplexer #(.enable("false")) demultiplexer_4 (
    .out0(demultiplexer_4_out0), .out1(Stop_t), .in(Loading_Inst_q), .sel(in_6));
  D_Flip_Flop #(.trigger("falling")) HALT (.clk(in_1), .D(or_5_out), .Q(Stop), .reset(in_2));  // open: Qn, preset, en
  or or_6 (CS, Chip_1, Chip_2);
  and and_1 (Write, Chip_2, in_5);
  or or_7 (PC_Address, Chip_1, Timer__Reset, PC);
  Demultiplexer #(.enable("false")) demultiplexer_5 (
    .out0(demultiplexer_5_out0), .out1(RAM), .in(demultiplexer_4_out0), .sel(in_4));

  // Other names for the same wires on the sheet: CLK = in_1; Halt = in_6; R_Time[3:0] = in_3; RAM_Inst = in_4;
  //   Ram_Reset = RAM; Reset = in_2; W_Time[3:0] = in_7; Write_t = in_5
endmodule
