// Logisim project s-mips_RE.circ as structural Verilog: 13 circuits, main circuit RAM
module S_MIPS_Board (
  input  DESHABILITAR_DISPATCHER,
  output halt
);

  wire button_1_out, CLK, CS, d_ff_1_q, LCLR, LoadRAM, LoadRAMOn, LW, R_R_W, R_W, ram_dispatcher_1_finished,
       RCS, Reset_out, RST, TTY_EN;
  wire [2:0] KDB;
  wire [3:0] LMask, Mask, ram_1_read_time, ram_1_write_time, RMask;
  wire [6:0] KDB_DATA, TTY_DATA;
  wire [15:0] Addr, LAddr, RAddr;
  wire [31:0] I0, I1, I2, I3, LData, ram_1_data_out_0, ram_1_data_out_1, ram_1_data_out_2, ram_1_data_out_3,
       RI0, RI1, RI2, RI3;

  TTY #(.rows(25), .cols(80)) tty_1 (.data(TTY_DATA), .clk(CLK), .we(TTY_EN), .clr(RST));
  not not_1 (LoadRAMOn, ram_dispatcher_1_finished);
  RAM_Dispatcher ram_dispatcher_1 (
    .WriteTime(ram_1_write_time), .Clock(CLK), .Data(LData), .Address(LAddr), .Mask(LMask),
    .Finished(ram_dispatcher_1_finished), .Write(LW), .CLR(LCLR));
  Keyboard #(.buflen(64)) keyboard_1 (.clk(CLK), .re(KDB[0]), .avail(KDB[2]), .data(KDB_DATA));  // open: clr
  RAM ram_1 (
    .Address(RAddr), .Data_Out_0(ram_1_data_out_0), .Data_Out_1(ram_1_data_out_1),
    .Data_Out_2(ram_1_data_out_2), .Data_Out_3(ram_1_data_out_3), .Data_In_0(RI0), .Data_In_1(RI1),
    .Data_In_2(RI2), .Data_In_3(RI3), .Mask(RMask), .nRead_Write(R_R_W), .Chip_Select(RCS),
    .Read_Time(ram_1_read_time), .Reset(button_1_out), .Write_Time(ram_1_write_time));
  Button button_1 (.out(button_1_out));
  D_Flip_Flop d_ff_1 (.clk(CLK), .D(1'b1), .Q(d_ff_1_q), .reset(Reset_out));  // open: Qn, preset, en
  Button Reset (.out(Reset_out));
  S_MIPS s_mips_1 (
    .Kbd_Enable(KDB[0]), .Address(Addr), .Kbd_Clear(KDB[1]), .Kbd_Available(KDB[2]), .RAM_In_0(I0),
    .Kbd_ASCII_Data(KDB_DATA), .RAM_In_1(I1), .TTY_Enable(TTY_EN), .RAM_In_2(I2), .RAM_In_3(I3),
    .TTY_ASCII_Data(TTY_DATA), .Reset(RST), .RAM_Out_0(ram_1_data_out_0), .Clock(CLK),
    .RAM_Out_1(ram_1_data_out_1), .Stop(halt), .RAM_Out_2(ram_1_data_out_2), .RAM_Out_3(ram_1_data_out_3),
    .Mask(Mask), .Read_Time(ram_1_read_time), .Write_Time(ram_1_write_time), .nRead_Write(R_W),
    .Chip_Select(CS));
  D_Flip_Flop d_ff_2 (.clk(CLK), .D(d_ff_1_q), .Qn(LCLR), .reset(Reset_out));  // open: Q, preset, en
  or or_1 (RST, LCLR, LoadRAM);
  Clock clock_1 (.out(CLK));
  Multiplexer #(.width(32), .enable("false")) multiplexer_1 (.in0(I0), .in1(LData), .out(RI0), .sel(LoadRAM));
  Multiplexer #(.width(32), .enable("false")) multiplexer_2 (.in0(I1), .in1(LData), .out(RI1), .sel(LoadRAM));
  Multiplexer #(.width(32), .enable("false")) multiplexer_3 (.in0(I2), .in1(LData), .out(RI2), .sel(LoadRAM));
  Multiplexer #(.width(32), .enable("false")) multiplexer_4 (.in0(I3), .in1(LData), .out(RI3), .sel(LoadRAM));
  and and_1 (LoadRAM, ~DESHABILITAR_DISPATCHER, LoadRAMOn);  // AND_Gate
  Multiplexer #(.width(16), .enable("false")) multiplexer_5 (.in0(Addr), .in1(LAddr), .out(RAddr), .sel(LoadRAM));
  Multiplexer #(.width(4), .enable("false")) multiplexer_6 (.in0(Mask), .in1(LMask), .out(RMask), .sel(LoadRAM));
  Multiplexer #(.enable("false")) multiplexer_7 (.in0(CS), .in1(LW), .out(RCS), .sel(LoadRAM));
  Multiplexer #(.enable("false")) multiplexer_8 (.in0(R_W), .in1(LW), .out(R_R_W), .sel(LoadRAM));

  // Notes on the sheet:
  //   NO MODIFICAR
  //   Keyboard
endmodule

module RAM (
  input  [15:0] Address,
  input  [31:0] Data_In_0,
  input  [31:0] Data_In_1,
  input  [31:0] Data_In_2,
  input  [31:0] Data_In_3,
  input  [3:0] Mask,
  input  nRead_Write,
  input  Chip_Select,
  input  Reset,
  output [31:0] Data_Out_0,
  output [31:0] Data_Out_1,
  output [31:0] Data_Out_2,
  output [31:0] Data_Out_3,
  output [3:0] Read_Time,
  output [3:0] Write_Time
);

  wire and_2_out, and_3_out, and_4_out, and_5_out, and_6_out, and_7_out, and_8_out, and_9_out, Changed, CLK,
       comparator_2_eq, comparator_3_eq, comparator_4_eq, comparator_5_eq, comparator_6_eq, Count,
       demultiplexer_3_out0, Idle, Idle_q, Load, Load0, Load1, nand_1_out, or_1_out, or_2_out, or_3_out,
       or_4_out, or_5_out, or_6_out, or_7_out, or_8_out, or_9_out, or_10_out, Proc_q, Update_Mem, Zero_Time;
  wire [3:0] counter_1_q, multiplexer_1_out, subtractor_1_out;
  wire [31:0] register_1_q, register_2_q, register_3_q, register_4_q, register_5_q;

  // Probe on 4'b0011
  // Probe on 4'b0010
  Multiplexer #(.width(4), .enable("false")) multiplexer_1 (
    .in0(4'b0011), .in1(4'b0010), .out(multiplexer_1_out), .sel(nRead_Write));
  or or_1 (or_1_out, Idle, Update_Mem);
  or or_2 (or_2_out, ~Chip_Select, Reset);  // OR_Gate
  Subtractor #(.width(4)) subtractor_1 (.a(multiplexer_1_out), .b(4'b0010), .out(subtractor_1_out));  // open: bin, bout
  Demultiplexer #(.enable("false")) demultiplexer_1 (.out0(Idle), .out1(Load0), .in(Idle_q), .sel(Changed));
  D_Flip_Flop u_Idle (.clk(CLK), .D(or_1_out), .Q(Idle_q), .preset(or_2_out));  // open: Qn, en, reset
  // Probe on counter_1_q
  Counter #(.width(4), .max('hf)) counter_1 (
    .load(Load), .D(subtractor_1_out), .count(Count), .Q(counter_1_q), .clk(CLK), .clr(or_3_out));  // open: carry
  or or_3 (or_3_out, ~Chip_Select, Reset);  // OR_Gate
  Comparator #(.width(4), .mode("unsigned")) comparator_1 (
    .a(4'b0000), .b(counter_1_q), .eq(Zero_Time));  // open: gt, lt
  or or_4 (or_4_out, Count, Load0, Load1);
  Register #(.width(32)) register_1 (.D(Data_In_0), .en(Chip_Select), .Q(register_1_q), .clk(CLK), .clr(or_5_out));
  or or_5 (or_5_out, ~Chip_Select, Reset);  // OR_Gate
  Register #(.width(32)) register_2 (.D(Data_In_1), .en(Chip_Select), .Q(register_2_q), .clk(CLK), .clr(or_6_out));
  or or_6 (or_6_out, ~Chip_Select, Reset);  // OR_Gate
  Register #(.width(32)) register_3 (.D(Data_In_2), .en(Chip_Select), .Q(register_3_q), .clk(CLK), .clr(or_7_out));
  or or_7 (or_7_out, ~Chip_Select, Reset);  // OR_Gate
  Register #(.width(32)) register_4 (.D(Data_In_3), .en(Chip_Select), .Q(register_4_q), .clk(CLK), .clr(or_8_out));
  or or_8 (or_8_out, ~Chip_Select, Reset);  // OR_Gate
  Register #(.width(32)) register_5 (
    .D({{11{1'b1}}, nRead_Write, Mask, Address}), .en(Chip_Select), .Q(register_5_q), .clk(CLK),
    .clr(or_9_out));
  or or_9 (or_9_out, ~Chip_Select, Reset);  // OR_Gate
  D_Flip_Flop Proc (.clk(CLK), .D(or_4_out), .Q(Proc_q), .reset(or_10_out));  // open: Qn, preset, en
  or or_10 (or_10_out, ~Chip_Select, Reset);  // OR_Gate
  Demultiplexer #(.enable("false")) demultiplexer_2 (
    .out0(Count), .out1(Update_Mem), .in(demultiplexer_3_out0), .sel(Zero_Time));
  Demultiplexer #(.enable("false")) demultiplexer_3 (
    .out0(demultiplexer_3_out0), .out1(Load1), .in(Proc_q), .sel(Changed));
  Clock clock_1 (.out(CLK));
  Comparator #(.width(32)) comparator_2 (.a(register_1_q), .b(Data_In_0), .eq(comparator_2_eq));  // open: gt, lt
  Comparator #(.width(32)) comparator_3 (.a(register_2_q), .b(Data_In_1), .eq(comparator_3_eq));  // open: gt, lt
  Comparator #(.width(32)) comparator_4 (.a(register_3_q), .b(Data_In_2), .eq(comparator_4_eq));  // open: gt, lt
  Comparator #(.width(32)) comparator_5 (.a(register_4_q), .b(Data_In_3), .eq(comparator_5_eq));  // open: gt, lt
  Comparator #(.width(32)) comparator_6 (
    .a(register_5_q), .b({{11{1'b1}}, nRead_Write, Mask, Address}), .eq(comparator_6_eq));  // open: gt, lt
  nand nand_1 (nand_1_out, comparator_6_eq, comparator_2_eq, comparator_3_eq, comparator_4_eq, comparator_5_eq);
  and and_1 (Changed, nand_1_out, Chip_Select);
  or or_11 (Load, Count, Load1, Load0);
  and and_2 (and_2_out, Mask[0], Update_Mem, nRead_Write);
  and and_3 (and_3_out, Mask[1], Update_Mem, nRead_Write);
  and and_4 (and_4_out, Mask[2], Update_Mem, nRead_Write);
  and and_5 (and_5_out, Mask[3], Update_Mem, nRead_Write);
  RAM_part #(.addrWidth(16), .dataWidth(32), .bus("separate")) ram_1 (
    .addr(Address), .din(Data_In_0), .data(Data_Out_0), .str(and_2_out), .sel(Chip_Select), .clk(CLK),
    .ld(and_6_out), .clr(Reset));
  and and_6 (and_6_out, ~nRead_Write, Idle);  // AND_Gate
  RAM_part #(.addrWidth(16), .dataWidth(32), .bus("separate")) ram_2 (
    .addr(Address), .din(Data_In_1), .data(Data_Out_1), .str(and_3_out), .sel(Chip_Select), .clk(CLK),
    .ld(and_7_out), .clr(Reset));
  and and_7 (and_7_out, ~nRead_Write, Idle);  // AND_Gate
  RAM_part #(.addrWidth(16), .dataWidth(32), .bus("separate")) ram_3 (
    .addr(Address), .din(Data_In_2), .data(Data_Out_2), .str(and_4_out), .sel(Chip_Select), .clk(CLK),
    .ld(and_8_out), .clr(Reset));
  and and_8 (and_8_out, ~nRead_Write, Idle);  // AND_Gate
  RAM_part #(.addrWidth(16), .dataWidth(32), .bus("separate")) ram_4 (
    .addr(Address), .din(Data_In_3), .data(Data_Out_3), .str(and_5_out), .sel(Chip_Select), .clk(CLK),
    .ld(and_9_out), .clr(Reset));
  and and_9 (and_9_out, ~nRead_Write, Idle);  // AND_Gate

  assign Read_Time = 4'b0011;
  assign Write_Time = 4'b0010;

  // Other names for the same wires on the sheet: M0 = Mask[0]; M1 = Mask[1]; M2 = Mask[2]; M3 = Mask[3];
  //   RW = nRead_Write; CLR = Reset; CS = Chip_Select; Load2 = Count

  // Notes on the sheet:
  //   NO MODIFICAR
  //   excepto quizás los valores RT y WT
  //   BANK0
  //   BANK1
  //   BANK2
  //   BANK3
endmodule

module S_MIPS (
  input  Kbd_Available,
  input  [6:0] Kbd_ASCII_Data,
  input  [31:0] RAM_Out_0,
  input  [31:0] RAM_Out_1,
  input  Reset,
  input  [31:0] RAM_Out_2,
  input  Clock,
  input  [31:0] RAM_Out_3,
  input  [3:0] Read_Time,
  input  [3:0] Write_Time,
  output Kbd_Enable,
  output [15:0] Address,
  output Kbd_Clear,
  output TTY_Enable,
  output [6:0] TTY_ASCII_Data,
  output Stop,
  output [31:0] RAM_In_0,
  output [31:0] RAM_In_1,
  output [31:0] RAM_In_2,
  output [31:0] RAM_In_3,
  output [3:0] Mask,
  output nRead_Write,
  output Chip_Select
);


  // Other names for the same wires on the sheet: CLK = Clock; CLR = Reset; CS = Chip_Select;
  //   KBD_AVAIL = Kbd_Available; KBD_CLR = Kbd_Clear; KBD_DATA[6:0] = Kbd_ASCII_Data; RAM_A[15:0] = Address;
  //   RAM_INPUT_0[31:0] = RAM_In_0; RAM_INPUT_1[31:0] = RAM_In_1; RAM_INPUT_2[31:0] = RAM_In_2;
  //   RAM_INPUT_3[31:0] = RAM_In_3; RAM_MASK[3:0] = Mask; RAM_OUTPUT_0[31:0] = RAM_Out_0;
  //   RAM_OUTPUT_1[31:0] = RAM_Out_1; RAM_OUTPUT_2[31:0] = RAM_Out_2; RAM_OUTPUT_3[31:0] = RAM_Out_3;
  //   RW = nRead_Write; TTY_DATA[6:0] = TTY_ASCII_Data

  // Notes on the sheet:
  //   RAM ADDRESS
  //   DATA FROM RAM
  //   DATA TO RAM
  //   DATA WRITE MASK
  //   RAM TIMING
  //   RAM CONTROL
  //   KEYBOARD
  //   TTY
  //   SEQUENCING
endmodule

module RAM_Dispatcher (
  input  [3:0] WriteTime,
  input  Clock,
  input  CLR,
  output [31:0] Data,
  output [15:0] Address,
  output [3:0] Mask,
  output Finished,
  output Write
);

  wire demultiplexer_2_out1, demultiplexer_3_out1, End, IDLE_q, IncAddr, Load, or_1_out, or_2_out, While_q,
       WriteEnd;
  wire [3:0] counter_1_q;
  wire [31:0] CurrentAddress_q;

  Counter #(.width(32), .max('hffffffff)) CurrentAddress (
    .count(IncAddr), .Q({CurrentAddress_q[31:18], Address, CurrentAddress_q[1:0]}), .clk(Clock), .clr(CLR));  // open: load, D, carry
  or or_1 (or_1_out, IncAddr, demultiplexer_3_out1, Finished);
  D_Flip_Flop IDLE (.clk(Clock), .D(or_1_out), .Q(IDLE_q), .preset(CLR));  // open: Qn, en, reset
  Demultiplexer #(.enable("false")) demultiplexer_1 (.out0(Load), .out1(Finished), .in(IDLE_q), .sel(End));
  D_Flip_Flop While (.clk(Clock), .D(or_2_out), .Q(While_q), .reset(CLR));  // open: Qn, preset, en
  or or_2 (or_2_out, Write, Load);
  RAM_part #(.addrWidth(18), .dataWidth(32)) ram_1 (
    .addr({Address, CurrentAddress_q[1:0]}), .data(Data), .clk(Clock));  // open: sel, ld, clr
  Demultiplexer #(.enable("false")) demultiplexer_2 (
    .out0(Write), .out1(demultiplexer_2_out1), .in(While_q), .sel(WriteEnd));
  Decoder #(.select(2)) decoder_1 (
    .out0(Mask[0]), .out1(Mask[1]), .out2(Mask[2]), .out3(Mask[3]), .sel(CurrentAddress_q[1:0]));  // open: en
  Demultiplexer #(.enable("false")) demultiplexer_3 (
    .out0(IncAddr), .out1(demultiplexer_3_out1), .in(demultiplexer_2_out1), .sel(End));
  Counter #(.width(4), .max('hf)) counter_1 (
    .load(Load), .D(WriteTime), .count(Write), .Q(counter_1_q), .clk(Clock));  // open: carry, clr
  Comparator #(.width(32)) comparator_1 (.a(Data), .b({32{1'b1}}), .eq(End));  // open: gt, lt
  Comparator #(.width(4)) comparator_2 (.a(4'b0000), .b(counter_1_q), .eq(WriteEnd));  // open: gt, lt

  // Other names for the same wires on the sheet: CLK = Clock; Count = Write; WT[3:0] = WriteTime
endmodule

module REGISTER_FILE (
  input  [4:0] RS_ADDRESS,
  input  WRITE,
  input  [4:0] RT_ADDRESS,
  input  [31:0] DATA_IN,
  input  CLK,
  input  [4:0] REG_TO_WRITE,
  input  CLR,
  input  EN,
  output [31:0] RT,
  output [31:0] RS
);

  wire and_1_out, LOAD_1, LOAD_2, LOAD_3, LOAD_4, LOAD_5, LOAD_6, LOAD_7, LOAD_8, LOAD_9, LOAD_10, LOAD_11,
       LOAD_12, LOAD_13, LOAD_14, LOAD_15, LOAD_16, LOAD_17, LOAD_18, LOAD_19, LOAD_20, LOAD_21, LOAD_22,
       LOAD_23, LOAD_24, LOAD_25, LOAD_26, LOAD_27, LOAD_28, LOAD_29, LOAD_30, LOAD_31;
  wire [31:0] R1, R2, R3, R4, R5, R6, R7, R8, R9, R10, R11, R12, R13, R14, R15, R16, R17, R18, R19, R20, R21,
       R22, R23, R24, R25, R26, R27, R28, R29, R30, R31;

  Multiplexer #(.select(5), .width(32), .enable("false")) multiplexer_1 (
    .in0({32{1'b0}}), .in1(R1), .in2(R2), .in3(R3), .in4(R4), .in5(R5), .in6(R6), .in7(R7), .in8(R8),
    .in9(R9), .in10(R10), .in11(R11), .in12(R12), .in13(R13), .in14(R14), .in15(R15), .in16(R16), .in17(R17),
    .in18(R18), .in19(R19), .in20(R20), .in21(R21), .in22(R22), .in23(R23), .in24(R24), .in25(R25),
    .in26(R26), .in27(R27), .in28(R28), .in29(R29), .in30(R30), .in31(R31), .out(RS), .sel(RS_ADDRESS));
  Register #(.width(32)) u_R1 (.D(DATA_IN), .en(LOAD_1), .Q(R1), .clk(CLK), .clr(CLR));
  Register #(.width(32)) u_R6 (.D(DATA_IN), .en(LOAD_6), .Q(R6), .clk(CLK), .clr(CLR));
  Register #(.width(32)) u_R11 (.D(DATA_IN), .en(LOAD_11), .Q(R11), .clk(CLK), .clr(CLR));
  Register #(.width(32)) u_R16 (.D(DATA_IN), .en(LOAD_16), .Q(R16), .clk(CLK), .clr(CLR));
  Register #(.width(32)) u_R21 (.D(DATA_IN), .en(LOAD_21), .Q(R21), .clk(CLK), .clr(CLR));
  Register #(.width(32)) u_R26 (.D(DATA_IN), .en(LOAD_26), .Q(R26), .clk(CLK), .clr(CLR));
  Register #(.width(32)) u_R31 (.D(DATA_IN), .en(LOAD_31), .Q(R31), .clk(CLK), .clr(CLR));
  Register #(.width(32)) u_R2 (.D(DATA_IN), .en(LOAD_2), .Q(R2), .clk(CLK), .clr(CLR));
  Register #(.width(32)) u_R7 (.D(DATA_IN), .en(LOAD_7), .Q(R7), .clk(CLK), .clr(CLR));
  Register #(.width(32)) u_R12 (.D(DATA_IN), .en(LOAD_12), .Q(R12), .clk(CLK), .clr(CLR));
  Register #(.width(32)) u_R17 (.D(DATA_IN), .en(LOAD_17), .Q(R17), .clk(CLK), .clr(CLR));
  Register #(.width(32)) u_R22 (.D(DATA_IN), .en(LOAD_22), .Q(R22), .clk(CLK), .clr(CLR));
  Register #(.width(32)) u_R27 (.D(DATA_IN), .en(LOAD_27), .Q(R27), .clk(CLK), .clr(CLR));
  Register #(.width(32)) u_R3 (.D(DATA_IN), .en(LOAD_3), .Q(R3), .clk(CLK), .clr(CLR));
  Register #(.width(32)) u_R8 (.D(DATA_IN), .en(LOAD_8), .Q(R8), .clk(CLK), .clr(CLR));
  Register #(.width(32)) u_R13 (.D(DATA_IN), .en(LOAD_13), .Q(R13), .clk(CLK), .clr(CLR));
  Register #(.width(32)) u_R18 (.D(DATA_IN), .en(LOAD_18), .Q(R18), .clk(CLK), .clr(CLR));
  Register #(.width(32)) u_R23 (.D(DATA_IN), .en(LOAD_23), .Q(R23), .clk(CLK), .clr(CLR));
  Register #(.width(32)) u_R28 (.D(DATA_IN), .en(LOAD_28), .Q(R28), .clk(CLK), .clr(CLR));
  Multiplexer #(.select(5), .width(32), .enable("false")) multiplexer_2 (
    .in0({32{1'b0}}), .in1(R1), .in2(R2), .in3(R3), .in4(R4), .in5(R5), .in6(R6), .in7(R7), .in8(R8),
    .in9(R9), .in10(R10), .in11(R11), .in12(R12), .in13(R13), .in14(R14), .in15(R15), .in16(R16), .in17(R17),
    .in18(R18), .in19(R19), .in20(R20), .in21(R21), .in22(R22), .in23(R23), .in24(R24), .in25(R25),
    .in26(R26), .in27(R27), .in28(R28), .in29(R29), .in30(R30), .in31(R31), .out(RT), .sel(RT_ADDRESS));
  Register #(.width(32)) u_R4 (.D(DATA_IN), .en(LOAD_4), .Q(R4), .clk(CLK), .clr(CLR));
  Register #(.width(32)) u_R9 (.D(DATA_IN), .en(LOAD_9), .Q(R9), .clk(CLK), .clr(CLR));
  Register #(.width(32)) u_R14 (.D(DATA_IN), .en(LOAD_14), .Q(R14), .clk(CLK), .clr(CLR));
  Register #(.width(32)) u_R19 (.D(DATA_IN), .en(LOAD_19), .Q(R19), .clk(CLK), .clr(CLR));
  Register #(.width(32)) u_R24 (.D(DATA_IN), .en(LOAD_24), .Q(R24), .clk(CLK), .clr(CLR));
  Register #(.width(32)) u_R29 (.D(DATA_IN), .en(LOAD_29), .Q(R29), .clk(CLK), .clr(CLR));
  Register #(.width(32)) u_R5 (.D(DATA_IN), .en(LOAD_5), .Q(R5), .clk(CLK), .clr(CLR));
  Register #(.width(32)) u_R10 (.D(DATA_IN), .en(LOAD_10), .Q(R10), .clk(CLK), .clr(CLR));
  Register #(.width(32)) u_R15 (.D(DATA_IN), .en(LOAD_15), .Q(R15), .clk(CLK), .clr(CLR));
  Register #(.width(32)) u_R20 (.D(DATA_IN), .en(LOAD_20), .Q(R20), .clk(CLK), .clr(CLR));
  Register #(.width(32)) u_R25 (.D(DATA_IN), .en(LOAD_25), .Q(R25), .clk(CLK), .clr(CLR));
  Register #(.width(32)) u_R30 (.D(DATA_IN), .en(LOAD_30), .Q(R30), .clk(CLK), .clr(CLR));
  and and_1 (and_1_out, WRITE, EN);
  Demultiplexer #(.select(5), .enable("false")) demultiplexer_1 (
    .out1(LOAD_1), .out2(LOAD_2), .out3(LOAD_3), .out4(LOAD_4), .out5(LOAD_5), .out6(LOAD_6), .out7(LOAD_7),
    .out8(LOAD_8), .out9(LOAD_9), .out10(LOAD_10), .out11(LOAD_11), .out12(LOAD_12), .out13(LOAD_13),
    .out14(LOAD_14), .out15(LOAD_15), .out16(LOAD_16), .out17(LOAD_17), .out18(LOAD_18), .out19(LOAD_19),
    .out20(LOAD_20), .out21(LOAD_21), .out22(LOAD_22), .out23(LOAD_23), .out24(LOAD_24), .out25(LOAD_25),
    .out26(LOAD_26), .out27(LOAD_27), .out28(LOAD_28), .out29(LOAD_29), .out30(LOAD_30), .out31(LOAD_31),
    .in(and_1_out), .sel(REG_TO_WRITE));  // open: out0

  // Notes on the sheet:
  //   R0
  //   R31/STACK POINTER
  //   GENERAL PURPOSE REGISTERS
endmodule

module ALU (
  input  [31:0] X,
  input  [31:0] Y,
  input  CLR,
  input  CLK,
  input  EN,
  input  [3:0] ALU_CONTROL,
  output DIV_BY_ZERO,
  output [31:0] OUT,
  output SIGN_FLAG,
  output ZERO_FLAG
);

  wire and_2_out, and_4_out, comparator_1_lt, comparator_2_lt, divisor_1_div_by_zero, DONE, DONE_DIV,
       DONE_DIV_DIVU, DONE_MULT_MULU, ENABLE_HI___LO, IS_DIV, IS_DIVU, IS_MULT, IS_MULU, IS_SLT, IS_SLTU,
       multiplexer_4_out, or_2_out, or_3_out, or_4_out, or_5_out, or_7_out, or_9_out, UNSIGNED;
  wire [31:0] ADD, AND, HI_DIV, HI_DIV_DIVU, HI_MULT, HI_MULT_MULU, HI_REG, LO_DIV, LO_DIV_DIVU, LO_MULT,
       LO_MULT_MULU, LO_REG, multiplexer_1_out, multiplexer_2_out, NOR, OR, SLT_SLTU, SUBSTRACT, XOR;

  // Probe on ALU_CONTROL
  Adder #(.width(32)) adder_1 (.a(X), .b(Y), .out(ADD));  // open: cin, cout
  Subtractor #(.width(32)) subtractor_1 (.a(X), .b(Y), .out(SUBSTRACT));  // open: bin, bout
  assign AND = X & Y;  // AND_Gate and_1, 32 bits wide
  assign OR = X | Y;  // OR_Gate or_1, 32 bits wide
  assign XOR = X ^ Y;  // XOR_Gate xor_1, 32 bits wide
  assign NOR = ~(X | Y);  // NOR_Gate nor_1, 32 bits wide
  or or_2 (or_2_out, IS_MULT, IS_MULU);
  and and_2 (and_2_out, ~DONE_MULT_MULU, or_2_out);  // AND_Gate
  Multiplexer #(.width(32), .enable("false")) multiplexer_1 (
    .in0(HI_MULT), .in1(HI_DIV), .out(multiplexer_1_out), .sel(or_3_out));
  or or_3 (or_3_out, IS_DIVU, IS_DIV);
  Multiplexer #(.width(32), .enable("false")) multiplexer_2 (
    .in0(LO_MULT), .in1(LO_DIV), .out(multiplexer_2_out), .sel(or_4_out));
  or or_4 (or_4_out, IS_DIVU, IS_DIV);
  MULTIPLIER multiplier_1 (
    .MULTIPLICAND(X), .MULTIPLIER(Y), .CLR(CLR), .START(and_2_out), .CLK(CLK), .DONE(DONE_MULT_MULU),
    .EN(EN), .LO(LO_MULT_MULU), .HI(HI_MULT_MULU), .UNSIGNED(UNSIGNED));
  Multiplexer #(.select(4), .width(32)) multiplexer_3 (
    .in0(ADD), .in1(SUBSTRACT), .in2(AND), .in3(OR), .in4(XOR), .in5(NOR), .in6(LO_REG), .in7(HI_REG),
    .in8(SLT_SLTU), .out(OUT), .sel(ALU_CONTROL), .en(EN));  // open: in9, in10, in11, in12, in13, in14, in15
  Register #(.width(32)) u_HI_REG (.D(multiplexer_1_out), .en(ENABLE_HI___LO), .Q(HI_REG), .clk(CLK), .clr(CLR));
  Register #(.width(32)) u_LO_REG (.D(multiplexer_2_out), .en(ENABLE_HI___LO), .Q(LO_REG), .clk(CLK), .clr(CLR));
  or or_5 (or_5_out, IS_DIV, IS_DIVU);
  or or_6 (UNSIGNED, IS_MULU, IS_SLTU, IS_DIVU);
  and and_3 (ENABLE_HI___LO, or_7_out, DONE);
  or or_7 (or_7_out, IS_MULT, IS_DIVU, IS_DIV, IS_MULU);
  Comparator #(.width(32)) comparator_1 (.a(SUBSTRACT), .b({32{1'b0}}), .lt(comparator_1_lt));  // open: gt, eq
  Comparator #(.width(32), .mode("unsigned")) comparator_2 (
    .a(SUBSTRACT), .b({32{1'b0}}), .lt(comparator_2_lt));  // open: gt, eq
  and and_4 (and_4_out, ~DONE_DIV, or_5_out);  // AND_Gate
  or or_8 (DONE, DONE_DIV_DIVU, DONE_MULT_MULU);
  Multiplexer #(.enable("false")) multiplexer_4 (
    .in0(comparator_1_lt), .in1(comparator_2_lt), .out(multiplexer_4_out), .sel(UNSIGNED));
  DIVISOR divisor_1 (
    .DIVIDEND(X), .DIVISOR(Y), .CLR(CLR), .CLK(CLK), .EN(EN), .START(and_4_out), .QUOTIENT(LO_DIV_DIVU),
    .DONE(DONE_DIV_DIVU), .DIV_BY_ZERO(divisor_1_div_by_zero), .REMAINDER(HI_DIV_DIVU), .UNSIGNED(UNSIGNED));
  or or_9 (or_9_out, IS_DIVU, IS_DIV);
  assign SLT_SLTU = {{31{1'b0}}, multiplexer_4_out};  // Bit_Extender bit_extender_1
  and and_5 (DIV_BY_ZERO, divisor_1_div_by_zero, or_9_out);
  Comparator #(.width(32), .mode("unsigned")) comparator_3 (.a(OUT), .b({32{1'b0}}), .eq(ZERO_FLAG));  // open: gt, lt
  Comparator #(.width(4)) comparator_4 (.a(ALU_CONTROL), .b(4'b1000), .eq(IS_SLT));  // open: gt, lt
  Comparator #(.width(4)) comparator_5 (.a(ALU_CONTROL), .b(4'b1001), .eq(IS_SLTU));  // open: gt, lt
  Comparator #(.width(4)) comparator_6 (.a(ALU_CONTROL), .b(4'b1010), .eq(IS_MULT));  // open: gt, lt
  Comparator #(.width(4)) comparator_7 (.a(ALU_CONTROL), .b(4'b1011), .eq(IS_MULU));  // open: gt, lt
  Comparator #(.width(4)) comparator_8 (.a(ALU_CONTROL), .b(4'b1100), .eq(IS_DIV));  // open: gt, lt
  Comparator #(.width(4)) comparator_9 (.a(ALU_CONTROL), .b(4'b1101), .eq(IS_DIVU));  // open: gt, lt

  assign SIGN_FLAG = OUT[31];
endmodule

module MULTIPLIER (
  input  [31:0] MULTIPLICAND,
  input  EN,
  input  UNSIGNED,
  input  CLR,
  input  CLK,
  input  START,
  input  [31:0] MULTIPLIER,
  output [31:0] HI,
  output [31:0] LO,
  output DONE
);

  wire and_1_out, and_2_out, and_3_out, and_4_out, and_5_out, and_6_out, and_8_out, and_9_out, and_13_out,
       and_14_out, B_OUT, C_OUT, ENABLE_REGISTERS, EXEC, INIT, NEXT_STATE__0, NEXT_STATE__1, or_1_out,
       or_2_out, or_3_out, or_6_out, or_7_out, or_8_out, Q___1, S_ADD, S_PASS, S_SUB, SIGN, STATE__0,
       STATE__1, xor_2_out, ZERO;
  wire [1:0] and_11_out, SIGN_SELECTOR;
  wire [31:0] A, A_M, A_M_t, M, multiplexer_1_out, multiplexer_2_out, multiplexer_3_out, Q, RESULT;

  // Probe on MULTIPLICAND
  // Probe on MULTIPLIER
  and and_1 (and_1_out, STATE__0, STATE__1);
  and and_2 (and_2_out, ~STATE__0, ~STATE__1);  // AND_Gate
  Counter #(.width(32), .max('h20)) CNT (.count(EXEC), .carry(ZERO), .clk(CLK), .clr(or_1_out));  // open: load, D, Q
  or or_1 (or_1_out, INIT, CLR);
  Multiplexer #(.width(32), .enable("false")) multiplexer_1 (
    .in0(MULTIPLICAND), .in1(M), .out(multiplexer_1_out), .sel(EXEC));
  Multiplexer #(.width(32), .enable("false")) multiplexer_2 (
    .in0({32{1'b0}}), .in1({SIGN, RESULT[31:1]}), .out(multiplexer_2_out), .sel(EXEC));
  or or_2 (or_2_out, and_1_out, and_2_out);
  or or_3 (or_3_out, START, ~STATE__1);  // OR_Gate
  Multiplexer #(.width(32), .enable("false")) multiplexer_3 (
    .in0(MULTIPLIER), .in1({RESULT[0], Q[31:1]}), .out(multiplexer_3_out), .sel(EXEC));
  Register #(.width(32), .trigger("falling")) u_A (
    .D(multiplexer_2_out), .en(ENABLE_REGISTERS), .Q(A), .clk(CLK), .clr(or_6_out));
  and and_3 (and_3_out, ZERO, ~STATE__0, STATE__1);  // AND_Gate
  or or_4 (NEXT_STATE__0, and_3_out, and_4_out);
  and and_4 (and_4_out, START, or_2_out);
  and and_5 (and_5_out, or_3_out, STATE__0);
  or or_5 (NEXT_STATE__1, and_5_out, and_6_out);
  and and_6 (and_6_out, ~STATE__0, STATE__1);  // AND_Gate
  Register #(.width(32), .trigger("falling")) u_M (
    .D(multiplexer_1_out), .en(ENABLE_REGISTERS), .Q(M), .clk(CLK), .clr(CLR));
  Register #(.width(32), .trigger("falling")) u_Q (
    .D(multiplexer_3_out), .en(ENABLE_REGISTERS), .Q(Q), .clk(CLK), .clr(CLR));
  or or_6 (or_6_out, INIT, CLR);
  and and_7 (INIT, ~STATE__1, STATE__0);  // AND_Gate
  Multiplexer #(.select(2), .width(32), .enable("false")) multiplexer_4 (
    .in0(A), .in1(A_M), .in2(A_M_t), .in3(A), .out(RESULT), .sel(SIGN_SELECTOR));
  D_Flip_Flop #(.trigger("falling")) u_Q___1 (
    .clk(CLK), .D(Q[0]), .Q(Q___1), .en(ENABLE_REGISTERS), .reset(or_7_out));  // open: Qn, preset
  Multiplexer #(.width(32), .enable("false")) multiplexer_5 (.in1(A), .out(HI), .sel(and_8_out));  // open: in0
  and and_8 (and_8_out, STATE__0, STATE__1);
  Multiplexer #(.width(32), .enable("false")) multiplexer_6 (.in1(Q), .out(LO), .sel(and_9_out));  // open: in0
  and and_9 (and_9_out, STATE__0, STATE__1);
  and and_10 (DONE, STATE__0, STATE__1);
  ExactlyOne xor_1 (.out(S_SUB), .in0(M[31]), .in1(A[31]), .in2(B_OUT));
  Adder #(.width(32)) adder_1 (.a(A), .b(M), .out(A_M), .cout(C_OUT));  // open: cin
  Subtractor #(.width(32)) subtractor_1 (.a(A), .b(M), .out(A_M_t), .bout(B_OUT));  // open: bin
  or or_7 (or_7_out, INIT, CLR);
  D_Flip_Flop #(.trigger("falling")) u_STATE__0 (
    .clk(CLK), .D(NEXT_STATE__0), .Q(STATE__0), .en(EN), .reset(CLR));  // open: Qn, preset
  D_Flip_Flop #(.trigger("falling")) u_STATE__1 (
    .clk(CLK), .D(NEXT_STATE__1), .Q(STATE__1), .en(EN), .reset(CLR));  // open: Qn, preset
  Multiplexer #(.enable("false")) multiplexer_7 (.in0(A[31]), .in1(1'b0), .out(S_PASS), .sel(UNSIGNED));
  and and_11 (and_11_out[0], ~Q[0], Q___1);  // AND_Gate
  and and_12 (and_11_out[1], ~Q___1, Q[0]);  // AND_Gate
  and and_13 (and_13_out, ~STATE__0, STATE__1);  // AND_Gate
  and and_14 (and_14_out, STATE__0, ~STATE__1);  // AND_Gate
  ExactlyOne xor_2 (.out(xor_2_out), .in0(M[31]), .in1(A[31]), .in2(C_OUT));
  Multiplexer #(.select(2), .enable("false")) multiplexer_8 (
    .in0(S_PASS), .in1(S_ADD), .in2(S_SUB), .in3(S_PASS), .out(SIGN), .sel(SIGN_SELECTOR));
  or or_8 (or_8_out, and_13_out, and_14_out);
  and and_15 (EXEC, ~STATE__0, STATE__1);  // AND_Gate
  Multiplexer #(.enable("false")) multiplexer_9 (.in0(xor_2_out), .in1(C_OUT), .out(S_ADD), .sel(UNSIGNED));
  Multiplexer #(.width(2), .enable("false")) multiplexer_10 (
    .in0(and_11_out), .in1({1'b0, Q[0]}), .out(SIGN_SELECTOR), .sel(UNSIGNED));
  and and_16 (ENABLE_REGISTERS, or_8_out, EN);

  // Other names for the same wires on the sheet: Q__0 = Q[0]

  // Notes on the sheet:
  //   INPUTS
  //   COUNTER
  //   PARTIAL REGISTERS
  //   TRANSITION FUNCTION (FSM)
  //   EXTRA BIT
  //   OUTPUTS
  //   STATES (FSM)
  //   EXIT FUNCTION (FSM)
endmodule

module DIVISOR (
  input  [31:0] DIVIDEND,
  input  [31:0] DIVISOR,
  input  CLK,
  input  CLR,
  input  EN,
  input  START,
  input  UNSIGNED,
  output [31:0] REMAINDER,
  output [31:0] QUOTIENT,
  output DONE,
  output DIV_BY_ZERO
);

  wire and_1_out, and_2_out, and_3_out, and_4_out, and_5_out, and_6_out, and_7_out, and_8_out, and_11_out,
       and_12_out, B_OUT, ENABLE_REGISTERS, EXEC, INIT, NEG_QUOTIENT, NEXT_STATE__0, NEXT_STATE__1, or_1_out,
       or_2_out, or_3_out, STATE__0, STATE__1, ZERO;
  wire [0:0] not_1_out;
  wire [31:0] A, ABS_DIVIDEND, ABS_DIVISOR, M, multiplexer_1_out, multiplexer_2_out, multiplexer_3_out,
       multiplexer_4_out, multiplexer_5_out, multiplexer_6_out, multiplexer_7_out, multiplexer_8_out,
       multiplexer_9_out, multiplexer_10_out, negator_1_out, negator_2_out, Q, SHIFTED_A__M;

  Counter #(.width(32), .max('h20)) CNT (.count(EXEC), .carry(ZERO), .clk(CLK), .clr(or_1_out));  // open: load, D, Q
  or or_1 (or_1_out, INIT, CLR);
  and and_1 (and_1_out, ~STATE__1, DIV_BY_ZERO);  // AND_Gate
  or or_2 (or_2_out, START, and_1_out);
  and and_2 (and_2_out, STATE__1, STATE__0);
  or or_3 (or_3_out, and_2_out, and_3_out);
  and and_3 (and_3_out, ~STATE__1, ~STATE__0);  // AND_Gate
  and and_4 (and_4_out, STATE__1, ~STATE__0);  // AND_Gate
  or or_4 (NEXT_STATE__1, and_4_out, and_5_out);
  and and_5 (and_5_out, STATE__0, or_2_out);
  and and_6 (and_6_out, STATE__1, ~STATE__0, ZERO);  // AND_Gate
  or or_5 (NEXT_STATE__0, and_6_out, and_7_out, and_8_out);
  and and_7 (and_7_out, ~STATE__1, STATE__0, DIV_BY_ZERO);  // AND_Gate
  and and_8 (and_8_out, START, or_3_out);
  Multiplexer #(.width(32), .enable("false")) multiplexer_1 (
    .in0(SHIFTED_A__M), .in1({A[30:0], Q[31]}), .out(multiplexer_1_out), .sel(B_OUT));
  Multiplexer #(.width(32), .enable("false")) multiplexer_2 (
    .in0(ABS_DIVISOR), .in1(DIVISOR), .out(multiplexer_2_out), .sel(UNSIGNED));
  Multiplexer #(.width(32), .enable("false")) multiplexer_3 (
    .in0(ABS_DIVIDEND), .in1(DIVIDEND), .out(multiplexer_3_out), .sel(UNSIGNED));
  not not_1 (not_1_out[0], B_OUT);
  Multiplexer #(.width(32), .enable("false")) multiplexer_4 (
    .in0({32{1'b0}}), .in1(multiplexer_1_out), .out(multiplexer_4_out), .sel(EXEC));
  Multiplexer #(.width(32), .enable("false")) multiplexer_5 (
    .in0(multiplexer_2_out), .in1(M), .out(multiplexer_5_out), .sel(EXEC));
  Multiplexer #(.width(32), .enable("false")) multiplexer_6 (
    .in0(multiplexer_3_out), .in1({Q[30:0], not_1_out[0]}), .out(multiplexer_6_out), .sel(EXEC));
  Register #(.width(32)) u_A (.D(multiplexer_4_out), .en(ENABLE_REGISTERS), .Q(A), .clk(CLK), .clr(CLR));
  Register #(.width(32)) u_M (.D(multiplexer_5_out), .en(ENABLE_REGISTERS), .Q(M), .clk(CLK), .clr(CLR));
  Register #(.width(32)) u_Q (.D(multiplexer_6_out), .en(ENABLE_REGISTERS), .Q(Q), .clk(CLK), .clr(CLR));
  D_Flip_Flop #(.trigger("falling")) u_STATE__0 (
    .clk(CLK), .D(NEXT_STATE__0), .Q(STATE__0), .en(EN), .reset(CLR));  // open: Qn, preset
  D_Flip_Flop #(.trigger("falling")) u_STATE__1 (
    .clk(CLK), .D(NEXT_STATE__1), .Q(STATE__1), .en(EN), .reset(CLR));  // open: Qn, preset
  Multiplexer #(.width(32), .enable("false")) multiplexer_7 (
    .in1(A), .out(multiplexer_7_out), .sel(DONE));  // open: in0
  Multiplexer #(.width(32), .enable("false")) multiplexer_8 (
    .in1(Q), .out(multiplexer_8_out), .sel(DONE));  // open: in0
  ABS abs_1 (.VALUE(DIVIDEND), .ABS_VALUE(ABS_DIVIDEND));
  ABS abs_2 (.VALUE(DIVISOR), .ABS_VALUE(ABS_DIVISOR));
  Negator #(.width(32)) negator_1 (.in(multiplexer_7_out), .out(negator_1_out));
  Negator #(.width(32)) negator_2 (.in(multiplexer_8_out), .out(negator_2_out));
  xor xor_1 (NEG_QUOTIENT, DIVIDEND[31], DIVISOR[31]);
  and and_9 (INIT, STATE__0, ~STATE__1);  // AND_Gate
  and and_10 (EXEC, ~STATE__0, STATE__1);  // AND_Gate
  Multiplexer #(.width(32), .enable("false")) multiplexer_9 (
    .in0(multiplexer_7_out), .in1(negator_1_out), .out(multiplexer_9_out), .sel(and_11_out));
  and and_11 (and_11_out, DONE, DIVIDEND[31], ~UNSIGNED);  // AND_Gate
  Multiplexer #(.width(32), .enable("false")) multiplexer_10 (
    .in0(multiplexer_8_out), .in1(negator_2_out), .out(multiplexer_10_out), .sel(and_12_out));
  and and_12 (and_12_out, DONE, NEG_QUOTIENT, ~UNSIGNED);  // AND_Gate
  or or_6 (ENABLE_REGISTERS, INIT, EXEC);
  Multiplexer #(.width(32), .enable("false")) multiplexer_11 (
    .in0(multiplexer_9_out), .in1(DIVIDEND), .out(REMAINDER), .sel(DIV_BY_ZERO));
  Multiplexer #(.width(32), .enable("false")) multiplexer_12 (
    .in0(multiplexer_10_out), .in1({32{1'b1}}), .out(QUOTIENT), .sel(DIV_BY_ZERO));
  and and_13 (DONE, STATE__0, STATE__1);
  Subtractor #(.width(32)) subtractor_1 (.a({A[30:0], Q[31]}), .b(M), .out(SHIFTED_A__M), .bout(B_OUT));  // open: bin
  Comparator #(.width(32)) comparator_1 (.a(DIVISOR), .b({32{1'b0}}), .eq(DIV_BY_ZERO));  // open: gt, lt

  // Other names for the same wires on the sheet: NEG_REMAINDER = DIVIDEND[31]; SHIFTED_A[31:0] = {A[30:0], Q[31]}

  // Notes on the sheet:
  //   INPUTS
  //   COUNTER
  //   TRANSITION FUNCTION (FSM)
  //   PARTIAL REGISTERS
  //   STATES (FSM)
  //   EXIT FUNCTION (FSM)
  //   OUTPUTS
endmodule

module ABS (
  input  [31:0] VALUE,
  output [31:0] ABS_VALUE
);

  wire [31:0] adder_1_out, not_1_out;

  assign not_1_out = ~VALUE;  // NOT_Gate not_1, 32 bits wide
  Adder #(.width(32)) adder_1 (.a(not_1_out), .b(32'h1), .out(adder_1_out));  // open: cin, cout
  Multiplexer #(.width(32), .enable("false")) multiplexer_1 (
    .in0(VALUE), .in1(adder_1_out), .out(ABS_VALUE), .sel(VALUE[31]));

  // Other names for the same wires on the sheet: X[31:0] = VALUE
endmodule

module PROGRAM_COUNTER (
  input  EN,
  input  CLK,
  input  CLR,
  input  [15:0] CONST,
  input  ZF,
  input  SF,
  input  IS_BEQ,
  input  IS_J,
  input  IS_BNE,
  input  IS_JR,
  input  IS_BLEZ,
  input  IS_BGTZ,
  input  [25:0] DEST,
  input  [31:0] RS,
  output [31:0] OUT
);

  wire and_1_out, and_2_out, and_3_out, and_4_out, and_5_out, CLK_t, or_1_out, or_2_out;
  wire [27:0] PC___4;
  wire [31:0] bit_extender_2_out, BRANCH_TARGET, JUMP_TARGET, multiplexer_1_out, multiplexer_2_out,
       multiplexer_3_out, PC, shifter_1_out;

  and and_1 (and_1_out, and_2_out, IS_BGTZ);
  and and_2 (and_2_out, ~ZF, ~SF);  // AND_Gate
  Clock clock_1 (.out(CLK_t));
  and and_3 (and_3_out, IS_BEQ, ZF);
  assign JUMP_TARGET[27:0] = {{2{DEST[25]}}, DEST};  // Bit_Extender bit_extender_1
  Multiplexer #(.width(32), .enable("false")) multiplexer_1 (
    .in0({JUMP_TARGET[31:28], PC___4}), .in1(BRANCH_TARGET), .out(multiplexer_1_out), .sel(or_1_out));
  or or_1 (or_1_out, and_1_out, and_3_out, and_4_out, and_5_out);
  and and_4 (and_4_out, IS_BNE, ~ZF);  // AND_Gate
  Multiplexer #(.width(32), .enable("false")) multiplexer_2 (
    .in0(multiplexer_1_out), .in1(JUMP_TARGET), .out(multiplexer_2_out), .sel(IS_J));
  and and_5 (and_5_out, IS_BLEZ, or_2_out);
  or or_2 (or_2_out, SF, ZF);
  assign bit_extender_2_out = {{16{CONST[15]}}, CONST};  // Bit_Extender bit_extender_2
  Multiplexer #(.width(32), .enable("false")) multiplexer_3 (
    .in0(multiplexer_2_out), .in1(RS), .out(multiplexer_3_out), .sel(IS_JR));
  // Probe on bit_extender_2_out
  Adder #(.width(32)) adder_1 (.a(PC), .b(32'h4), .out({JUMP_TARGET[31:28], PC___4}));  // open: cin, cout
  Register #(.width(32)) u_PC (.D(multiplexer_3_out), .en(EN), .Q(OUT), .clk(CLK_t), .clr(CLR));
  Shifter #(.width(32)) shifter_1 (.in(bit_extender_2_out), .\dist (5'b00010), .out(shifter_1_out));
  Adder #(.width(32)) adder_2 (
    .a(shifter_1_out), .b({JUMP_TARGET[31:28], PC___4}), .out(BRANCH_TARGET));  // open: cin, cout

  // Other names for the same wires on the sheet: PC___4[31:28] = JUMP_TARGET[31:28]
endmodule

module CONTROL_UNIT (
  input  [31:0] INSTRUCTION,
  output [15:0] CONST,
  output [25:0] DEST,
  output [4:0] RD,
  output [4:0] RT,
  output [4:0] RS,
  output IS_BEQ,
  output IS_BNE,
  output IS_BLEZ,
  output IS_BGTZ,
  output IS_JR,
  output IS_J,
  output REG_WRITE,
  output ALU_SRC,
  output EXT_OP,
  output REG_DEST,
  output [1:0] MEM_TO_REG,
  output [3:0] ALU_CONTROL,
  output IS_LW,
  output IS_PUSH,
  output IS_SW,
  output IS_POP,
  output IS_HALT
);

  wire ADD, ADDI, AND, and_1_out, and_3_out, and_4_out, ANDI, BLTZ, DIV, DIVU, HALT_TTY_KBD_RND, JUMP, KBD,
       MEM_READ, MEM_WRITE, MFHI, MFLO, MULT, MULU, NOP, NOR, not_1_out, OR, ORI, PUSH_POP, RND, SLT, SLTI,
       SLTIU, SLTU, SUB, TIPO_R, TTY, XOR, XORI;

  not not_1 (not_1_out, INSTRUCTION[31]);
  and and_1 (and_1_out, HALT_TTY_KBD_RND, ~INSTRUCTION[5]);  // AND_Gate
  and and_2 (IS_HALT, INSTRUCTION[5], HALT_TTY_KBD_RND);
  Decoder #(.select(5), .disabled(0)) decoder_1 (
    .out0(TIPO_R), .out1(BLTZ), .out2(IS_J), .out4(IS_BEQ), .out5(IS_BNE), .out6(IS_BLEZ), .out7(IS_BGTZ),
    .out8(ADDI), .out10(SLTI), .out11(SLTIU), .out12(ANDI), .out13(ORI), .out14(XORI),
    .sel(INSTRUCTION[30:26]), .en(not_1_out));  // open: out3, out9, out15, out16, out17, out18, out19, out20, out21, out22, out23, out24, out25, out26, out27, out28, out29, out30, out31
  Decoder #(.select(5), .disabled(0)) decoder_2 (
    .out3(IS_LW), .out11(IS_SW), .out24(PUSH_POP), .out31(HALT_TTY_KBD_RND), .sel(INSTRUCTION[30:26]),
    .en(INSTRUCTION[31]));  // open: out0, out1, out2, out4, out5, out6, out7, out8, out9, out10, out12, out13, out14, out15, out16, out17, out18, out19, out20, out21, out22, out23, out25, out26, out27, out28, out29, out30
  Decoder #(.select(5), .disabled(0)) decoder_3 (
    .out1(TTY), .out2(RND), .out4(KBD), .sel(INSTRUCTION[4:0]), .en(and_1_out));  // open: out0, out3, out5, out6, out7, out8, out9, out10, out11, out12, out13, out14, out15, out16, out17, out18, out19, out20, out21, out22, out23, out24, out25, out26, out27, out28, out29, out30, out31
  and and_3 (and_3_out, TIPO_R, ~INSTRUCTION[5]);  // AND_Gate
  and and_4 (and_4_out, INSTRUCTION[5], TIPO_R);
  Decoder #(.select(5), .disabled(0)) decoder_4 (
    .out0(NOP), .out4(IS_JR), .out16(MFHI), .out18(MFLO), .out24(MULT), .out25(MULU), .out26(DIV),
    .out27(DIVU), .sel(INSTRUCTION[4:0]), .en(and_3_out));  // open: out1, out2, out3, out5, out6, out7, out8, out9, out10, out11, out12, out13, out14, out15, out17, out19, out20, out21, out22, out23, out28, out29, out30, out31
  Decoder #(.select(5), .disabled(0)) decoder_5 (
    .out0(ADD), .out2(SUB), .out4(AND), .out5(OR), .out7(NOR), .out8(XOR), .out10(SLT), .out11(SLTU),
    .sel(INSTRUCTION[4:0]), .en(and_4_out));  // open: out1, out3, out6, out9, out12, out13, out14, out15, out16, out17, out18, out19, out20, out21, out22, out23, out24, out25, out26, out27, out28, out29, out30, out31
  or or_1 (REG_WRITE, MFHI, KBD, RND, IS_POP, IS_LW, XORI, ORI, ANDI, MFLO, ADD, SUB, AND, OR, SLT, SLTU, ADDI, SLTI, SLTIU);
  and and_5 (IS_PUSH, PUSH_POP, INSTRUCTION[0]);
  and and_6 (IS_POP, PUSH_POP, ~INSTRUCTION[0]);  // AND_Gate
  or or_2 (JUMP, IS_J, IS_JR);
  // Probe on INSTRUCTION
  or or_3 (EXT_OP, ADDI, XORI, ORI);
  or or_4 (ALU_SRC, SLTIU, SLTI, ADDI, IS_LW, ORI, ANDI, IS_SW, XORI);
  or or_5 (REG_DEST, IS_POP, TIPO_R, KBD, RND);
  or or_6 (MEM_WRITE, IS_PUSH, IS_SW);
  or or_7 (MEM_READ, IS_LW, IS_POP);
  or or_8 (MEM_TO_REG[0], KBD, IS_POP, IS_LW);
  or or_9 (MEM_TO_REG[1], RND, KBD);
  or or_10 (ALU_CONTROL[0], IS_BEQ, IS_BNE, IS_BLEZ, IS_BGTZ, MULU, SLTIU, NOR, OR, SUB, ORI, MFHI, SLTU);
  or or_11 (ALU_CONTROL[1], MULT, MFLO, ORI, AND, ANDI, OR, MFHI, MULU);
  or or_12 (ALU_CONTROL[2], DIVU, MFLO, XORI, XOR, NOR, MFHI, DIV);
  or or_13 (ALU_CONTROL[3], DIV, MULT, SLT, SLTI, SLTIU, SLTU, MULU, DIVU);

  assign CONST = INSTRUCTION[15:0];
  assign DEST = INSTRUCTION[25:0];
  assign RD = INSTRUCTION[15:11];
  assign RS = INSTRUCTION[25:21];
  assign RT = INSTRUCTION[20:16];

  // Other names for the same wires on the sheet: BEQ = IS_BEQ; BGTZ = IS_BGTZ; BLEZ = IS_BLEZ; BNE = IS_BNE;
  //   HALT = IS_HALT; FUNC_CODE[5:0] = INSTRUCTION[5:0]; INST[31:0] = INSTRUCTION; OPCODE[5:0] = INSTRUCTION[31:26];
  //   J = IS_J; JR = IS_JR; LW = IS_LW; POP = IS_POP; PUSH = IS_PUSH; SW = IS_SW
endmodule

module CIRCUIT (
  input  [31:0] RAM_Out_0,
  input  [31:0] RAM_Out_1,
  input  [31:0] RAM_Out_2,
  input  [31:0] RAM_Out_3,
  input  Kbd_Available,
  input  [6:0] Kbd_ASCII_Data,
  input  [1:0] BANK_SEL,
  input  EN,
  input  CLK,
  input  CLR,
  output [31:0] RAM_In_0,
  output [15:0] RAM_ADDR,
  output [31:0] RAM_In_1,
  output CS,
  output [31:0] RAM_In_2,
  output [31:0] RAM_In_3,
  output R_W,
  output [3:0] Mask
);

  wire ADDR_SEL, ALU_SRC, CLK_t, clock_1_out, DIV_BY_ZERO, EXT_OP, IS_BEQ, IS_BGTZ, IS_BLEZ, IS_BNE, IS_HALT,
       IS_J, IS_JR, IS_LW, IS_POP, IS_PUSH, IS_SW, REG_DEST, REG_WRITE, SF, ZF;
  wire [1:0] MEM_TO_REG;
  wire [3:0] ALU_CONTROL;
  wire [4:0] multiplexer_1_out, RD, RS, RT;
  wire [15:0] CONST;
  wire [25:0] DEST;
  wire [31:0] ALU_OUT, bit_extender_1_out, bit_extender_2_out, bit_extender_3_out, DATA_IN,
       multiplexer_2_out, multiplexer_3_out, multiplexer_4_out, PC, register_1_q, RND_DATA, RS_t,
       SELECTED_RAM_OUTPUT;

  assign bit_extender_1_out = {{16{CONST[15]}}, CONST};  // Bit_Extender bit_extender_1
  assign bit_extender_2_out = {{16{1'b0}}, CONST};  // Bit_Extender bit_extender_2
  Random #(.width(32)) random_1 (.clk(CLK_t), .next(EN), .out(RND_DATA), .clr(CLR));
  Multiplexer #(.width(5), .enable("false")) multiplexer_1 (
    .in0(RT), .in1(RD), .out(multiplexer_1_out), .sel(REG_DEST));
  Clock clock_1 (.out(clock_1_out));
  and and_1 (CLK_t, clock_1_out, ~IS_HALT);  // AND_Gate
  Multiplexer #(.width(32), .enable("false")) multiplexer_2 (
    .in0(bit_extender_1_out), .in1(bit_extender_2_out), .out(multiplexer_2_out), .sel(EXT_OP));
  Multiplexer #(.width(32), .enable("false")) multiplexer_3 (
    .in0(RAM_In_0), .in1(multiplexer_2_out), .out(multiplexer_3_out), .sel(ALU_SRC));
  assign bit_extender_3_out = {{25{1'b0}}, Kbd_ASCII_Data};  // Bit_Extender bit_extender_3
  Multiplexer #(.width(32), .enable("false")) multiplexer_4 (
    .in0({32{1'b1}}), .in1(bit_extender_3_out), .out(multiplexer_4_out), .sel(Kbd_Available));
  REGISTER_FILE register_file_1 (
    .RS_ADDRESS(RS), .WRITE(REG_WRITE), .RT_ADDRESS(RT), .DATA_IN(DATA_IN), .REG_TO_WRITE(multiplexer_1_out),
    .CLR(CLR), .RT(RAM_In_0), .RS(RS_t), .CLK(CLK_t), .EN(EN));
  ALU alu_1 (
    .X(RS_t), .Y(multiplexer_3_out), .CLR(CLR), .EN(EN), .ALU_CONTROL(ALU_CONTROL),
    .DIV_BY_ZERO(DIV_BY_ZERO), .OUT(ALU_OUT), .ZERO_FLAG(ZF), .SIGN_FLAG(SF), .CLK(CLK_t));
  Multiplexer #(.select(2), .width(32), .enable("false")) multiplexer_5 (
    .in0(ALU_OUT), .in1(SELECTED_RAM_OUTPUT), .in2(RND_DATA), .in3(multiplexer_4_out), .out(DATA_IN),
    .sel(MEM_TO_REG));
  Multiplexer #(.select(2), .width(32)) multiplexer_6 (
    .in0(RAM_Out_0), .in1(RAM_Out_1), .in2(RAM_Out_2), .in3(RAM_Out_3), .out(SELECTED_RAM_OUTPUT),
    .sel(BANK_SEL));  // open: en
  Multiplexer #(.width(2)) multiplexer_7 (
    .in0(PC[3:2]), .in1(ALU_OUT[3:2]), .out(BANK_SEL), .sel(ADDR_SEL));  // open: en
  Multiplexer #(.width(16)) multiplexer_8 (
    .in0(PC[19:4]), .in1(ALU_OUT[19:4]), .out(RAM_ADDR), .sel(ADDR_SEL));  // open: en
  or or_1 (ADDR_SEL, IS_PUSH, IS_LW, IS_SW, IS_POP);
  Decoder #(.select(2)) decoder_1 (
    .out0(Mask[0]), .out1(Mask[1]), .out2(Mask[2]), .out3(Mask[3]), .sel(BANK_SEL));  // open: en
  Register #(.width(32)) register_1 (.D(SELECTED_RAM_OUTPUT), .en(EN), .Q(register_1_q), .clk(CLK_t), .clr(CLR));
  CONTROL_UNIT control_unit_1 (
    .INSTRUCTION(register_1_q), .ALU_CONTROL(ALU_CONTROL), .CONST(CONST), .DEST(DEST), .IS_BEQ(IS_BEQ),
    .IS_BNE(IS_BNE), .IS_BLEZ(IS_BLEZ), .IS_BGTZ(IS_BGTZ), .IS_J(IS_J), .IS_JR(IS_JR), .RD(RD), .RT(RT),
    .RS(RS), .REG_WRITE(REG_WRITE), .ALU_SRC(ALU_SRC), .EXT_OP(EXT_OP), .REG_DEST(REG_DEST),
    .MEM_TO_REG(MEM_TO_REG), .IS_LW(IS_LW), .IS_PUSH(IS_PUSH), .IS_SW(IS_SW), .IS_POP(IS_POP),
    .IS_HALT(IS_HALT));
  PROGRAM_COUNTER program_counter_1 (
    .EN(EN), .CLK(CLK_t), .CLR(CLR), .CONST(CONST), .ZF(ZF), .SF(SF), .IS_BEQ(IS_BEQ), .IS_J(IS_J),
    .IS_BNE(IS_BNE), .IS_JR(IS_JR), .IS_BLEZ(IS_BLEZ), .IS_BGTZ(IS_BGTZ), .DEST(DEST), .RS(RS_t), .OUT(PC));
  or or_2 (CS, IS_LW, IS_PUSH, IS_SW, IS_POP);
  or or_3 (R_W, IS_PUSH, IS_SW);

  assign RAM_In_1 = RAM_In_0;
  assign RAM_In_2 = RAM_In_0;
  assign RAM_In_3 = RAM_In_0;

  // Other names for the same wires on the sheet: KBD_AVAIL = Kbd_Available; KBD_DATA[6:0] = Kbd_ASCII_Data;
  //   RAM_MASK[3:0] = Mask; RAM_OUTPUT_0[31:0] = RAM_Out_0; RAM_OUTPUT_1[31:0] = RAM_Out_1;
  //   RAM_OUTPUT_2[31:0] = RAM_Out_2; RAM_OUTPUT_3[31:0] = RAM_Out_3; RAM_INPUT_0[31:0] = RAM_In_0;
  //   RAM_INPUT_1[31:0] = RAM_In_0; RAM_INPUT_2[31:0] = RAM_In_0; RAM_INPUT_3[31:0] = RAM_In_0; RT_t[31:0] = RAM_In_0
endmodule

module TEST (
);

  ROM rom_1 ();  // open: addr, data, sel
endmodule
